// Logisim project T1.circ as structural Verilog: 1 circuit, main circuit main
module main (
);

  DotMatrix #(.inputtype("row"), .matrixcols(16), .matrixrows(16)) dotmatrix_1 (
    .row0(16'h100), .row1(16'hf908), .row2(16'h908), .row3(16'h910), .row4(16'h920), .row5(16'h7940),
    .row6(16'h4100), .row7(16'h47fe), .row8(16'h4140), .row9(16'h7920), .row10(16'h920), .row11(16'h910),
    .row12(16'h908), .row13(16'h944), .row14(16'h5182), .row15(16'h2100));
  DotMatrix #(.inputtype("row"), .matrixcols(16), .matrixrows(16)) dotmatrix_2 (
    .row0(16'h820), .row1(16'h820), .row2(16'hfffe), .row3(16'h820), .row4(16'h820), .row5(16'h100),
    .row6(16'h100), .row7(16'h100), .row8(16'h1100), .row9(16'h11f8), .row10(16'h1100), .row11(16'h1100),
    .row12(16'h1100), .row13(16'h1100), .row14(16'hfffe), .row15({16{1'b0}}));
  DotMatrix #(.inputtype("row"), .matrixcols(16), .matrixrows(16)) dotmatrix_3 (
    .row0(16'h820), .row1(16'h820), .row2(16'hfffe), .row3(16'h820), .row4(16'h820), .row5(16'h100),
    .row6(16'h3ff8), .row7(16'h2108), .row8(16'h2108), .row9(16'h3ff8), .row10(16'h2108), .row11(16'h2108),
    .row12(16'hfffe), .row13(16'h2008), .row14(16'h2028), .row15(16'h2010));
endmodule
