// Logisim project T4.circ as structural Verilog
module AND_gate (
  input  in_1,
  input  in_2,
  output out_3
);

  wire transistor_1_out;

  Transistor #(.\type ("n")) transistor_1 (.in(1'b1), .out(transistor_1_out), .gate(in_1));
  Transistor #(.\type ("n")) transistor_2 (.in(transistor_1_out), .out(out_3), .gate(in_2));
  Transistor transistor_3 (.in(1'b0), .out(out_3), .gate(in_2));
  Transistor transistor_4 (.in(1'b0), .out(out_3), .gate(in_1));

  // Notes on the sheet:
  //   与门
  //   张芷苒_PB21081601
endmodule

module OR_gate (
  input  in_1,
  input  in_2,
  output out_3
);

  wire transistor_3_out;

  Transistor #(.\type ("n")) transistor_1 (.in(1'b1), .out(out_3), .gate(in_1));
  Transistor transistor_2 (.in(transistor_3_out), .out(out_3), .gate(in_2));
  Transistor transistor_3 (.in(1'b0), .out(transistor_3_out), .gate(in_1));
  Transistor #(.\type ("n")) transistor_4 (.in(1'b1), .out(out_3), .gate(in_2));

  // Notes on the sheet:
  //   或门
  //   张芷苒_PB21081601
endmodule

module NOT_gate (
  input  in_1,
  output out_2
);

  Transistor transistor_1 (.in(1'b1), .out(out_2), .gate(in_1));
  Transistor #(.\type ("n")) transistor_2 (.in(1'b0), .out(out_2), .gate(in_1));

  // Notes on the sheet:
  //   非门
  //   张芷苒_PB21081601
endmodule

module _1_bit_2_1_mux (
  input  D0,
  input  S,
  input  D1,
  output Y
);

  wire and_gate_1_out_3, and_gate_2_out_3, not_gate_1_out_2;

  NOT_gate not_gate_1 (.in_1(S), .out_2(not_gate_1_out_2));
  AND_gate and_gate_1 (.in_1(D0), .in_2(not_gate_1_out_2), .out_3(and_gate_1_out_3));
  AND_gate and_gate_2 (.in_1(S), .in_2(D1), .out_3(and_gate_2_out_3));
  OR_gate or_gate_1 (.in_1(and_gate_1_out_3), .in_2(and_gate_2_out_3), .out_3(Y));

  // Notes on the sheet:
  //   1 bit 二选一选择器
  //   张芷苒_PB21081601
  //   总计：2个与门，1个或门，1个非门。
endmodule

module _2_bit_4_1_mux (
  input  [1:0] D0,
  input  [1:0] D1,
  input  [1:0] D2,
  input  [1:0] D3,
  input  S1,
  input  S0,
  output [1:0] Y
);

  _1_bit_4_1_mux u_1_bit_4_1_mux_1 (.S1(S1), .S0(S0), .D0(D0[0]), .D1(D1[0]), .D2(D2[0]), .D3(D3[0]));  // open: Y
  _1_bit_4_1_mux u_1_bit_4_1_mux_2 (.S1(S1), .S0(S0), .D0(D0[1]), .D1(D1[1]), .D2(D2[1]), .D3(D3[1]));  // open: Y

  // Notes on the sheet:
  //   2 bit 四选一选择器
  //   张芷苒_PB21081601
  //   Y0
  //   Y1
  //   总计：12个与门，6个或门，6个非门。
endmodule

module _1_bit_4_1_mux (
  input  S1,
  input  S0,
  input  D0,
  input  D1,
  input  D2,
  input  D3,
  output Y
);

  wire n1_bit_2_1_mux_1_y, n1_bit_2_1_mux_2_y;

  _1_bit_2_1_mux u_1_bit_2_1_mux_1 (.D0(D0), .S(S0), .D1(D1), .Y(n1_bit_2_1_mux_1_y));
  _1_bit_2_1_mux u_1_bit_2_1_mux_2 (.D0(D2), .S(S0), .D1(D3), .Y(n1_bit_2_1_mux_2_y));
  _1_bit_2_1_mux u_1_bit_2_1_mux_3 (.D0(n1_bit_2_1_mux_1_y), .S(S1), .D1(n1_bit_2_1_mux_2_y), .Y(Y));

  // Notes on the sheet:
  //   1 bit 四选一选择器
  //   Y0
  //   Y1
endmodule
