// Logisim project lab3.circ as structural Verilog: 17 circuits, main circuit main
module main (
  input  D,
  input  nRST,
  output Q,
  output out_4
);

  wire and_1_out, clock_1_out;

  Clock clock_1 (.out(clock_1_out));
  and and_1 (and_1_out, D, nRST);
  \D触发器  \d触发器_1  (.D(clock_1_out), .out_3(Q), .out_4(out_4), .CLK(and_1_out));

  // Notes on the sheet:
  //   有时钟的同步复位D触发器
  //   同步复位D触发器，理论上来说，只有当reset为1时
  //   一旦reset了0，D再变都没有用
  //   电路才有机会等于D的值，并且只有在D变化与时钟上升沿同步时Q才会输出D的值。
  //   RESET的变化也要与时钟上升沿同步才有效，变为1开闸，变为0就是把Q置为0
endmodule

module \双稳电路  (
  input  in_1,
  input  in_2,
  output out_3,
  output out_4,
  output out_5,
  output out_6
);

  not not_1 (out_3, out_5);
  not not_2 (out_5, out_3);
  not not_3 (out_4, out_6);
  not not_4 (out_6, out_4);
endmodule

module \SR锁存器  (
  input  R,
  input  S,
  output Q,
  output nQ
);

  nor nor_1 (Q, R, nQ);
  nor nor_2 (nQ, Q, S);

  // Notes on the sheet:
  //   初次使用要充电！
  //   任何状态变成r0s0：保持原状态
  //   任何状态变成r1s0：reset, \q1q0
  //   任何状态变成r0s1：set, q1\q0
  //   有1为1时，另外一个不能为1
endmodule

module \D锁存器  (
  input  CLK,
  input  D,
  output Q,
  output nQ
);

  wire and_1_out, and_2_out, not_1_out;

  not not_1 (not_1_out, D);
  and and_1 (and_1_out, CLK, not_1_out);
  and and_2 (and_2_out, CLK, D);
  nor nor_1 (Q, and_1_out, nQ);
  nor nor_2 (nQ, Q, and_2_out);

  // Notes on the sheet:
  //   D锁存器必须要先给CLK通了电才能用
endmodule

module \D触发器  (
  input  CLK,
  input  D,
  output out_3,
  output out_4
);

  wire \d锁存器_1_q , not_1_out;

  not not_1 (not_1_out, CLK);
  \D锁存器  \d锁存器_1  (.CLK(not_1_out), .D(D), .Q(\d锁存器_1_q ));  // open: nQ
  \D锁存器  \d锁存器_2  (.CLK(CLK), .D(\d锁存器_1_q ), .Q(out_3), .nQ(out_4));

  // Notes on the sheet:
  //   信号，瞬间传输
  //   第二个D锁存器要先初始化CLK的输入再接上前面来的线，否则相当于买了电器没通电
  //   为触发器添加复位信号，当复位信号（低电平）有效时，Q始终为0.->转同步复位的D触发器
endmodule

module \同步复位寄存器  (
  input  [3:0] D_IN,
  input  in_2,
  input  RST_N,
  output [3:0] D_OUT
);

  wire and_1_out, and_2_out, and_3_out, and_4_out;

  and and_1 (and_1_out, RST_N, D_IN[0]);
  and and_2 (and_2_out, RST_N, D_IN[1]);
  and and_3 (and_3_out, RST_N, D_IN[2]);
  and and_4 (and_4_out, RST_N, D_IN[3]);
  D_Flip_Flop d_ff_1 (.clk(in_2), .D(and_1_out), .Q(D_OUT[0]));  // open: Qn, preset, en, reset
  D_Flip_Flop d_ff_2 (.clk(in_2), .D(and_2_out), .Q(D_OUT[1]));  // open: Qn, preset, en, reset
  D_Flip_Flop d_ff_3 (.clk(in_2), .D(and_3_out), .Q(D_OUT[2]));  // open: Qn, preset, en, reset
  D_Flip_Flop d_ff_4 (.clk(in_2), .D(and_4_out), .Q(D_OUT[3]));  // open: Qn, preset, en, reset

  // Notes on the sheet:
  //   瞬间传输
  //   带有低电平有效的同步复位信号
endmodule

module \简单时序逻辑电路  (
  input  in_1,
  output [3:0] out_2
);

  wire clock_1_out;
  wire [3:0] adder_1_out;

  Clock clock_1 (.out(clock_1_out));
  Adder #(.width(4)) adder_1 (.a(out_2), .b(4'b0001), .out(adder_1_out), .cin(1'b0));  // open: cout
  \同步复位寄存器  \u_同步复位寄存器_1  (.D_IN(adder_1_out), .RST_N(in_1), .D_OUT(out_2), .in_2(clock_1_out));
endmodule

module T1 (
  input  \R非 ,
  input  \S非 ,
  output Q,
  output nQ
);

  nand nand_1 (Q, \R非 , nQ);
  nand nand_2 (nQ, Q, \S非 );
endmodule

module T2 (
  input  D,
  input  rst,
  input  rst_n,
  output Q,
  output out_5
);

  wire clock_1_out, \d锁存器_1_q , n2_1_mux_1_out, n2_1_mux_2_out, not_1_out;

  Clock clock_1 (.out(clock_1_out));
  not not_1 (not_1_out, clock_1_out);
  _2_1_MUX u_2_1_mux_1 (.d0(D), .s(rst_n), .d1(n2_1_mux_2_out), .out(n2_1_mux_1_out));
  _2_1_MUX u_2_1_mux_2 (.d0(1'b0), .s(rst), .d1(1'b1), .out(n2_1_mux_2_out));
  \D锁存器  \d锁存器_1  (.CLK(not_1_out), .D(n2_1_mux_1_out), .Q(\d锁存器_1_q ));  // open: nQ
  \D锁存器  \d锁存器_2  (.CLK(clock_1_out), .D(\d锁存器_1_q ), .Q(Q), .nQ(out_5));

  // Notes on the sheet:
  //   temp1
  //   temp2
endmodule

module _2_1_MUX (
  input  d0,
  input  s,
  input  d1,
  output out
);

  wire and_1_out, and_2_out, not_1_out;

  not not_1 (not_1_out, s);
  and and_1 (and_1_out, d0, not_1_out);
  and and_2 (and_2_out, s, d1);
  or or_1 (out, and_1_out, and_2_out);

  // Notes on the sheet:
  //   carry0
  //   carry 1
  //   carry 2
endmodule

module \同步复位D触发器  (
  input  CLK,
  input  D,
  input  nRST,
  output Q,
  output out_5
);

  wire and_1_out;

  and and_1 (and_1_out, D, nRST);
  \D触发器  \d触发器_1  (.D(CLK), .out_3(Q), .out_4(out_5), .CLK(and_1_out));

  // Notes on the sheet:
  //   瞬间点击
endmodule

module \异步复位D触发器  (
  input  CLK,
  input  D,
  input  CLR,
  output Q,
  output nQ
);

  D_Flip_Flop d_ff_1 (.clk(CLK), .D(D), .Q(Q), .Qn(nQ), .reset(CLR));  // open: preset, en

  // Notes on the sheet:
  //   CLR是复位键，高电平有效，不管时钟信号和输入信号是什么，只要CLR有效，输出就变成0(低电平)
endmodule

module \异步复位寄存器  (
  input  [3:0] D_IN,
  input  CLK,
  input  CLR,
  output [3:0] D_OUT
);

  \异步复位D触发器  \u_异步复位d触发器_1  (.CLK(CLK), .D(D_IN[0]), .CLR(CLR), .Q(D_OUT[0]));  // open: nQ
  \异步复位D触发器  \u_异步复位d触发器_2  (.CLK(CLK), .D(D_IN[1]), .CLR(CLR), .Q(D_OUT[1]));  // open: nQ
  \异步复位D触发器  \u_异步复位d触发器_3  (.CLK(CLK), .D(D_IN[2]), .CLR(CLR), .Q(D_OUT[2]));  // open: nQ
  \异步复位D触发器  \u_异步复位d触发器_4  (.CLK(CLK), .D(D_IN[3]), .CLR(CLR), .Q(D_OUT[3]));  // open: nQ
endmodule

module T3 (
  input  CLR,
  output [3:0] counter
);

  wire CLK_out;
  wire [3:0] adder_1_out;

  Clock CLK (.out(CLK_out));
  Adder #(.width(4)) adder_1 (.a(counter), .b(4'b0001), .out(adder_1_out), .cin(1'b0));  // open: cout
  \异步复位寄存器  \u_异步复位寄存器_1  (.D_IN(adder_1_out), .CLR(CLR), .D_OUT(counter), .CLK(CLK_out));
endmodule

module T4 (
  input  clr,
  output Q0,
  output Q1,
  output Q2,
  output Q3
);

  wire and_1_out, and_2_out, clk_out, FF0_qn, FF1_qn, FF2_qn, multiplexer_1_out, multiplexer_2_out,
       nor_1_out, not_1_out;

  Clock clk (.out(clk_out));
  not not_1 (not_1_out, clk_out);
  nor nor_1 (nor_1_out, Q0, Q1, Q2, Q3);
  T_Flip_Flop FF0 (.clk(not_1_out), .T(1'b1), .Q(Q0), .Qn(FF0_qn), .reset(clr));  // open: preset, en
  Multiplexer multiplexer_1 (.in0(FF0_qn), .in1(1'b0), .out(multiplexer_1_out), .sel(nor_1_out));  // open: en
  T_Flip_Flop FF1 (.clk(not_1_out), .T(multiplexer_1_out), .Q(Q1), .Qn(FF1_qn), .reset(clr));  // open: preset, en
  and and_1 (and_1_out, FF0_qn, FF1_qn);
  Multiplexer multiplexer_2 (.in0(and_1_out), .in1(1'b0), .out(multiplexer_2_out), .sel(nor_1_out));  // open: en
  T_Flip_Flop FF2 (.clk(not_1_out), .T(multiplexer_2_out), .Q(Q2), .Qn(FF2_qn), .reset(clr));  // open: preset, en
  and and_2 (and_2_out, and_1_out, FF2_qn);
  T_Flip_Flop FF3 (.clk(not_1_out), .T(and_2_out), .Q(Q3), .reset(clr));  // open: Qn, preset, en

  // Notes on the sheet:
  //   置位判断门
  //   clk_n
  //   低位
  //   rst
  //   t1=Q[0]
  //   selout 1
  //   t2
  //   selout 2
  //   t3
  //   高位
endmodule

module T5 (
  input  D,
  input  RST,
  output Q,
  output out_4
);

  wire and_1_out, CLK_out, not_1_out;

  Clock CLK (.out(CLK_out));
  not not_1 (not_1_out, RST);
  and and_1 (and_1_out, D, not_1_out);
  \D触发器  \d触发器_1  (.D(CLK_out), .out_3(Q), .out_4(out_4), .CLK(and_1_out));

  // Notes on the sheet:
  //   RST==1，复位，不过有延迟
endmodule

module test (
  input  D,
  input  CLR,
  output Q,
  output nQ
);

  wire clock_1_out;

  Clock clock_1 (.out(clock_1_out));
  D_Flip_Flop d_ff_1 (.clk(clock_1_out), .D(D), .Q(Q), .Qn(nQ), .reset(CLR));  // open: preset, en
endmodule
