// Logisim project lab06.circ as structural Verilog
module step3 (
  input  in_1,
  input  in_2,
  output out_3
);

  wire clock_1_out, d_ff_1_q, ram_1_data;

  Clock clock_1 (.out(clock_1_out));
  RAM #(.addrWidth(2), .dataWidth(1)) ram_1 (.addr({in_1, in_2}), .data(ram_1_data));  // open: sel, clk, ld, clr
  D_Flip_Flop d_ff_1 (.clk(clock_1_out), .D(ram_1_data), .Q(d_ff_1_q));  // open: Qn, preset, en, reset
  Multiplexer multiplexer_1 (.in0(d_ff_1_q), .in1(ram_1_data), .out(out_3), .sel(1'b1));  // open: en
endmodule
