// Logisim project lab06t1.circ as structural Verilog
module t1 (
  input  in_1,
  input  in_2,
  input  a,
  input  b,
  output out_5,
  output out_6,
  output out_7,
  output A_2,
  output B_2
);

  wire buffer_1_out, buffer_2_out, clock_1_out, d_ff_1_q, decoder_1_out1, decoder_1_out2, decoder_1_out3,
       decoder_2_out1, decoder_2_out2, decoder_2_out3, decoder_3_out1, decoder_3_out2, decoder_3_out3,
       multiplexer_2_out, multiplexer_3_out;
  wire [0:0] multiplexer_1_out;

  Clock clock_1 (.out(clock_1_out));
  Multiplexer multiplexer_1 (.in0(out_5), .in1(a), .out(multiplexer_1_out[0]), .sel(1'b0));  // open: en
  Multiplexer #(.select(2)) multiplexer_2 (
    .in0(1'b0), .in1(1'b1), .in2(1'b1), .in3(1'b0), .out(multiplexer_2_out), .sel({b, multiplexer_1_out[0]}));  // open: en
  D_Flip_Flop d_ff_1 (.clk(clock_1_out), .D(multiplexer_2_out), .Q(d_ff_1_q));  // open: Qn, preset, en, reset
  Multiplexer multiplexer_3 (.in0(d_ff_1_q), .in1(multiplexer_2_out), .out(multiplexer_3_out), .sel(1'b0));  // open: en
  Decoder #(.select(2)) decoder_1 (
    .out1(decoder_1_out1), .out2(decoder_1_out2), .out3(decoder_1_out3), .sel(2'b11));  // open: out0, en
  assign out_5 = decoder_1_out1 ? in_1 : 1'bz;  // Controlled_Buffer controlled_buffer_1
  assign out_5 = decoder_1_out2 ? in_2 : 1'bz;  // Controlled_Buffer controlled_buffer_2
  assign out_5 = decoder_1_out3 ? multiplexer_3_out : 1'bz;  // Controlled_Buffer controlled_buffer_3
  assign out_6 = decoder_2_out1 ? in_1 : 1'bz;  // Controlled_Buffer controlled_buffer_4
  assign out_6 = decoder_2_out2 ? in_2 : 1'bz;  // Controlled_Buffer controlled_buffer_5
  assign out_6 = decoder_2_out3 ? multiplexer_3_out : 1'bz;  // Controlled_Buffer controlled_buffer_6
  Decoder #(.select(2)) decoder_2 (
    .out1(decoder_2_out1), .out2(decoder_2_out2), .out3(decoder_2_out3), .sel(2'b01));  // open: out0, en
  Decoder #(.select(2)) decoder_3 (
    .out1(decoder_3_out1), .out2(decoder_3_out2), .out3(decoder_3_out3), .sel(2'b11));  // open: out0, en
  assign out_7 = decoder_3_out1 ? in_1 : 1'bz;  // Controlled_Buffer controlled_buffer_7
  assign out_7 = decoder_3_out2 ? in_2 : 1'bz;  // Controlled_Buffer controlled_buffer_8
  assign out_7 = decoder_3_out3 ? multiplexer_3_out : 1'bz;  // Controlled_Buffer controlled_buffer_9
  buf buffer_1 (buffer_1_out, A_2);
  assign A_2 = 1'b1 ? out_6 : 1'bz;  // Controlled_Buffer controlled_buffer_10
  buf buffer_2 (buffer_2_out, B_2);
  assign B_2 = 1'b1 ? out_7 : 1'bz;  // Controlled_Buffer controlled_buffer_11
endmodule
