// Logisim project lab8.circ as structural Verilog: 3 circuits, main circuit main
module main (
  input  sw,
  input  rst,
  output out_3,
  output out_4,
  output out_5,
  output out_6,
  output [3:0] out_7
);

  wire and_1_out, and_2_out, and_3_out, and_4_out, clock_1_out, d_ff_1_q, d_ff_2_q, d_ff_3_q, d_ff_4_q,
       multiplexer_1_out, multiplexer_2_out, multiplexer_3_out, multiplexer_4_out, not_1_out, not_2_out,
       not_3_out, or_1_out, xor_1_out, xor_2_out, xor_3_out, xor_4_out;

  Clock clock_1 (.out(clock_1_out));
  not not_1 (not_1_out, sw);
  D_Flip_Flop d_ff_1 (.clk(clock_1_out), .D(sw), .Q(d_ff_1_q));  // open: Qn, preset, en, reset
  D_Flip_Flop d_ff_2 (.clk(clock_1_out), .D(not_1_out), .Q(d_ff_2_q));  // open: Qn, preset, en, reset
  D_Flip_Flop d_ff_3 (.clk(clock_1_out), .D(d_ff_1_q), .Q(d_ff_3_q));  // open: Qn, preset, en, reset
  D_Flip_Flop d_ff_4 (.clk(clock_1_out), .D(d_ff_2_q), .Q(d_ff_4_q));  // open: Qn, preset, en, reset
  not not_2 (not_2_out, d_ff_3_q);
  not not_3 (not_3_out, d_ff_4_q);
  and and_1 (and_1_out, not_2_out, d_ff_1_q);
  and and_2 (and_2_out, not_3_out, d_ff_2_q);
  or or_1 (or_1_out, and_1_out, and_2_out);
  xor xor_1 (xor_1_out, 1'b1, out_3);
  Multiplexer multiplexer_1 (.in0(out_3), .in1(xor_1_out), .out(multiplexer_1_out), .sel(or_1_out));  // open: en
  D_Flip_Flop d_ff_5 (.clk(clock_1_out), .D(multiplexer_1_out), .Q(out_3), .reset(rst));  // open: Qn, preset, en
  xor xor_2 (xor_2_out, out_3, out_4);
  Multiplexer multiplexer_2 (.in0(out_4), .in1(xor_2_out), .out(multiplexer_2_out), .sel(or_1_out));  // open: en
  D_Flip_Flop d_ff_6 (.clk(clock_1_out), .D(multiplexer_2_out), .Q(out_4), .reset(rst));  // open: Qn, preset, en
  and and_3 (and_3_out, out_3, out_4);
  xor xor_3 (xor_3_out, and_3_out, out_5);
  Multiplexer multiplexer_3 (.in0(out_5), .in1(xor_3_out), .out(multiplexer_3_out), .sel(or_1_out));  // open: en
  D_Flip_Flop d_ff_7 (.clk(clock_1_out), .D(multiplexer_3_out), .Q(out_5), .reset(rst));  // open: Qn, preset, en
  and and_4 (and_4_out, and_3_out, out_5);
  Multiplexer multiplexer_4 (.in0(out_6), .in1(xor_4_out), .out(multiplexer_4_out), .sel(or_1_out));  // open: en
  xor xor_4 (xor_4_out, and_4_out, out_6);
  D_Flip_Flop d_ff_8 (.clk(clock_1_out), .D(multiplexer_4_out), .Q(out_6), .reset(rst));  // open: Qn, preset, en

  assign out_7 = {out_3, out_4, out_5, out_6};

  // Notes on the sheet:
  //   从左至右为低位至高位
endmodule

module lab8t2 (
  input  in_1,
  input  in_2,
  input  rst,
  output [3:0] out_4
);

  wire and_1_out, and_2_out, and_3_out, and_4_out, clock_1_out, d_ff_1_q, d_ff_2_q, not_1_out, not_2_out,
       or_1_out;

  Clock clock_1 (.out(clock_1_out));
  D_Flip_Flop d_ff_1 (.clk(clock_1_out), .D(in_1), .Q(d_ff_1_q));  // open: Qn, preset, en, reset
  D_Flip_Flop d_ff_2 (.clk(clock_1_out), .D(d_ff_1_q), .Q(d_ff_2_q));  // open: Qn, preset, en, reset
  not not_1 (not_1_out, d_ff_2_q);
  not not_2 (not_2_out, d_ff_1_q);
  and and_1 (and_1_out, not_1_out, d_ff_1_q);
  and and_2 (and_2_out, not_2_out, d_ff_2_q);
  or or_1 (or_1_out, and_1_out, and_2_out);
  D_Flip_Flop d_ff_3 (.clk(or_1_out), .D(in_2), .Q(out_4[0]), .reset(rst));  // open: Qn, preset, en
  D_Flip_Flop d_ff_4 (.clk(or_1_out), .D(out_4[0]), .Q(out_4[1]));  // open: Qn, preset, en, reset
  and and_3 (and_3_out, out_4[1], out_4[0]);
  D_Flip_Flop d_ff_5 (.clk(or_1_out), .D(and_3_out), .Q(out_4[2]), .reset(rst));  // open: Qn, preset, en
  and and_4 (and_4_out, out_4[2], and_3_out);
  D_Flip_Flop d_ff_6 (.clk(or_1_out), .D(and_4_out), .Q(out_4[3]), .reset(rst));  // open: Qn, preset, en
endmodule

module D_FlipFlop (
  input  CLK,
  input  D,
  output Q,
  output nQ
);

  wire and_1_out, and_2_out, not_1_out;

  not not_1 (not_1_out, D);
  and and_1 (and_1_out, CLK, not_1_out);
  and and_2 (and_2_out, CLK, D);
  nor nor_1 (Q, and_1_out, nQ);
  nor nor_2 (nQ, Q, and_2_out);
endmodule
