// Logisim project 2led+滚动 .circ as structural Verilog: 2 circuits, main circuit main
module main (
);

  wire [8:0] \n0_f计数器_1_out_1 ;
  wire [15:0] rom_1_data, rom_2_data, rom_3_data, rom_4_data, rom_5_data, rom_6_data, rom_7_data, rom_8_data,
       rom_9_data, rom_10_data, rom_11_data, rom_12_data, rom_13_data, rom_14_data, rom_15_data, rom_16_data,
       rom_17_data, rom_18_data, rom_19_data, rom_20_data, rom_21_data, rom_22_data, rom_23_data,
       rom_24_data, rom_25_data, rom_26_data, rom_27_data, rom_28_data, rom_29_data, rom_30_data,
       rom_31_data, rom_32_data;

  \_0_f计数器  \u_0_f计数器_1  (.out_1(\n0_f计数器_1_out_1 ));
  ROM #(.addrWidth(9), .dataWidth(16)) rom_1 (.addr(\n0_f计数器_1_out_1 ), .data(rom_1_data));  // open: sel
  ROM #(.addrWidth(9), .dataWidth(16)) rom_2 (.addr(\n0_f计数器_1_out_1 ), .data(rom_2_data));  // open: sel
  ROM #(.addrWidth(9), .dataWidth(16)) rom_3 (.addr(\n0_f计数器_1_out_1 ), .data(rom_3_data));  // open: sel
  ROM #(.addrWidth(9), .dataWidth(16)) rom_4 (.addr(\n0_f计数器_1_out_1 ), .data(rom_4_data));  // open: sel
  ROM #(.addrWidth(9), .dataWidth(16)) rom_5 (.addr(\n0_f计数器_1_out_1 ), .data(rom_5_data));  // open: sel
  ROM #(.addrWidth(9), .dataWidth(16)) rom_6 (.addr(\n0_f计数器_1_out_1 ), .data(rom_6_data));  // open: sel
  ROM #(.addrWidth(9), .dataWidth(16)) rom_7 (.addr(\n0_f计数器_1_out_1 ), .data(rom_7_data));  // open: sel
  ROM #(.addrWidth(9), .dataWidth(16)) rom_8 (.addr(\n0_f计数器_1_out_1 ), .data(rom_8_data));  // open: sel
  ROM #(.addrWidth(9), .dataWidth(16)) rom_9 (.addr(\n0_f计数器_1_out_1 ), .data(rom_9_data));  // open: sel
  ROM #(.addrWidth(9), .dataWidth(16)) rom_10 (.addr(\n0_f计数器_1_out_1 ), .data(rom_10_data));  // open: sel
  ROM #(.addrWidth(9), .dataWidth(16)) rom_11 (.addr(\n0_f计数器_1_out_1 ), .data(rom_11_data));  // open: sel
  ROM #(.addrWidth(9), .dataWidth(16)) rom_12 (.addr(\n0_f计数器_1_out_1 ), .data(rom_12_data));  // open: sel
  ROM #(.addrWidth(9), .dataWidth(16)) rom_13 (.addr(\n0_f计数器_1_out_1 ), .data(rom_13_data));  // open: sel
  ROM #(.addrWidth(9), .dataWidth(16)) rom_14 (.addr(\n0_f计数器_1_out_1 ), .data(rom_14_data));  // open: sel
  ROM #(.addrWidth(9), .dataWidth(16)) rom_15 (.addr(\n0_f计数器_1_out_1 ), .data(rom_15_data));  // open: sel
  ROM #(.addrWidth(9), .dataWidth(16)) rom_16 (.addr(\n0_f计数器_1_out_1 ), .data(rom_16_data));  // open: sel
  ROM #(.addrWidth(9), .dataWidth(16)) rom_17 (.addr(\n0_f计数器_1_out_1 ), .data(rom_17_data));  // open: sel
  ROM #(.addrWidth(9), .dataWidth(16)) rom_18 (.addr(\n0_f计数器_1_out_1 ), .data(rom_18_data));  // open: sel
  ROM #(.addrWidth(9), .dataWidth(16)) rom_19 (.addr(\n0_f计数器_1_out_1 ), .data(rom_19_data));  // open: sel
  ROM #(.addrWidth(9), .dataWidth(16)) rom_20 (.addr(\n0_f计数器_1_out_1 ), .data(rom_20_data));  // open: sel
  ROM #(.addrWidth(9), .dataWidth(16)) rom_21 (.addr(\n0_f计数器_1_out_1 ), .data(rom_21_data));  // open: sel
  ROM #(.addrWidth(9), .dataWidth(16)) rom_22 (.addr(\n0_f计数器_1_out_1 ), .data(rom_22_data));  // open: sel
  ROM #(.addrWidth(9), .dataWidth(16)) rom_23 (.addr(\n0_f计数器_1_out_1 ), .data(rom_23_data));  // open: sel
  ROM #(.addrWidth(9), .dataWidth(16)) rom_24 (.addr(\n0_f计数器_1_out_1 ), .data(rom_24_data));  // open: sel
  ROM #(.addrWidth(9), .dataWidth(16)) rom_25 (.addr(\n0_f计数器_1_out_1 ), .data(rom_25_data));  // open: sel
  ROM #(.addrWidth(9), .dataWidth(16)) rom_26 (.addr(\n0_f计数器_1_out_1 ), .data(rom_26_data));  // open: sel
  ROM #(.addrWidth(9), .dataWidth(16)) rom_27 (.addr(\n0_f计数器_1_out_1 ), .data(rom_27_data));  // open: sel
  ROM #(.addrWidth(9), .dataWidth(16)) rom_28 (.addr(\n0_f计数器_1_out_1 ), .data(rom_28_data));  // open: sel
  ROM #(.addrWidth(9), .dataWidth(16)) rom_29 (.addr(\n0_f计数器_1_out_1 ), .data(rom_29_data));  // open: sel
  ROM #(.addrWidth(9), .dataWidth(16)) rom_30 (.addr(\n0_f计数器_1_out_1 ), .data(rom_30_data));  // open: sel
  ROM #(.addrWidth(9), .dataWidth(16)) rom_31 (.addr(\n0_f计数器_1_out_1 ), .data(rom_31_data));  // open: sel
  ROM #(.addrWidth(9), .dataWidth(16)) rom_32 (.addr(\n0_f计数器_1_out_1 ), .data(rom_32_data));  // open: sel
  DotMatrix #(.inputtype("row"), .matrixcols(16), .matrixrows(16)) dotmatrix_1 (
    .row0(rom_1_data), .row1(rom_2_data), .row2(rom_3_data), .row3(rom_4_data), .row4(rom_5_data),
    .row5(rom_6_data), .row6(rom_7_data), .row7(rom_8_data), .row8(rom_9_data), .row9(rom_10_data),
    .row10(rom_11_data), .row11(rom_12_data), .row12(rom_13_data), .row13(rom_14_data), .row14(rom_15_data),
    .row15(rom_16_data));
  DotMatrix #(.inputtype("row"), .matrixcols(16), .matrixrows(16)) dotmatrix_2 (
    .row0(rom_17_data), .row1(rom_18_data), .row2(rom_19_data), .row3(rom_20_data), .row4(rom_21_data),
    .row5(rom_22_data), .row6(rom_23_data), .row7(rom_24_data), .row8(rom_25_data), .row9(rom_26_data),
    .row10(rom_27_data), .row11(rom_28_data), .row12(rom_29_data), .row13(rom_30_data), .row14(rom_31_data),
    .row15(rom_32_data));

  // Notes on the sheet:
  //   2-2
  //   2-3
  //   2-4
  //   2-6
  //   2-7
  //   2-8
  //   2-9
  //   2-10
  //   2-13
  //   2-14
  //   2-15
  //   1
  //   2
  //   3
  //   4
  //   5
  //   6
  //   7
  //   8
  //   9
  //   10
  //   11
  //   12
  //   13
  //   14
  //   15
  //   16
  //   2-1
  //   2-5
  //   2-11
  //   2-12
  //   2-16
  //   contents of rom_1 (hex, n*v repeats v):
  //   8*0 8000 4000 2000 1000 800 400 200 100 80 40 20 10 8 4 2 1 13*0 8000 c000 e000 f000 f800 fc00 fe00
  //   ff00 ff80 7fc0 3fe0 1ff0 ff8 7fc 3fe 1ff ff 7f 3f 1f f 7 3 1 106*0 8000 4000 2000 1000 800 400 8200
  //   4100 2080 1040 820 410 208 104 82 41 20 10 8 4 2 1 9*0 8000 4000 2000 1000 800 400 8200 4100 2080
  //   1040 820 410 208 104 82 41 20 10 8 4 2 1 13*0 8000 4000 2000 1000 800 400 200 100 80 40 20 10 8 4 2
  //   1 16*0 8000 4000 2000 1000 800 400 200 100 80 40 20 10 8 4 2 1 16*0 8000 4000 2000 9000 4800 2400
  //   1200 900 480 240 120 90 48 24 12 9 4 2 1 11*0 8000 4000 2000 1000 8800 4400 2200 1100 880 440 220
  //   110 88 44 22 11 8 4 2 1
  //   contents of rom_2 (hex, n*v repeats v):
  //   7*0 8000 4000 2000 1000 800 400 200 8100 4080 2040 1020 810 408 204 102 81 40 20 10 8 4 2 1 7*0 8000
  //   4000 2000 1000 800 400 200 100 8080 4040 2020 1010 808 404 202 101 80 40 20 10 8 4 2 1 106*0 8000
  //   4000 2000 1000 800 400 8200 4100 2080 1040 820 410 208 104 82 41 20 10 8 4 2 1 9*0 8000 4000 2000
  //   9000 4800 2400 9200 4900 2480 9240 4920 2490 1248 924 492 249 124 92 49 24 12 9 4 2 1 10*0 8000 4000
  //   2000 1000 800 400 200 100 80 40 20 10 8 4 2 1 16*0 8000 4000 2000 1000 800 400 200 100 80 40 20 10 8
  //   4 2 1 16*0 8000 4000 2000 9000 4800 2400 1200 900 480 240 120 90 48 24 12 9 4 2 1 11*0 8000 4000
  //   2000 1000 8800 4400 2200 1100 880 440 220 110 88 44 22 11 8 4 2 1
  //   contents of rom_3 (hex, n*v repeats v):
  //   7*0 8000 4000 2000 1000 800 400 8200 4100 2080 1040 820 410 208 104 82 41 20 10 8 4 2 1 8*0 8000
  //   4000 2000 1000 800 400 200 100 8080 4040 2020 1010 808 404 202 101 80 40 20 10 8 4 2 1 106*0 8000
  //   4000 2000 1000 800 400 200 8100 4080 2040 1020 810 408 204 102 81 40 20 10 8 4 2 1 8*0 8000 4000
  //   2000 1000 8800 4400 a200 5100 a880 5440 2a20 1510 a88 544 2a2 151 a8 54 2a 15 a 5 2 1 11*0 8000 4000
  //   2000 1000 800 400 200 100 80 40 20 10 8 4 2 1 16*0 8000 4000 2000 1000 800 400 200 100 80 40 20 10 8
  //   4 2 1 16*0 8000 4000 2000 9000 4800 2400 1200 900 480 240 120 90 48 24 12 9 4 2 1 11*0 8000 4000
  //   2000 1000 8800 4400 2200 1100 880 440 220 110 88 44 22 11 8 4 2 1
  //   contents of rom_4 (hex, n*v repeats v):
  //   0 0 0 8000 c000 e000 f000 f800 fc00 fe00 ff00 ff80 7fc0 bfe0 5ff0 2ff8 17fc bfe 5ff 2ff 17f bf 5f 2f
  //   17 b 5 2 1 8*0 8000 c000 e000 f000 f800 fc00 fe00 ff00 ff80 7fc0 3fe0 1ff0 ff8 7fc 3fe 1ff ff 7f 3f
  //   1f f 7 3 1 102*0 8000 c000 e000 f000 f800 7c00 3e00 9f00 cf80 e7c0 f3e0 f9f0 fcf8 7e7c 3f3e 1f9f fcf
  //   7e7 3f3 1f9 fc 7e 3f 1f f 7 3 1 0 0 0 8000 c000 e000 f000 f800 7c00 3e00 1f00 f80 7c0 83e0 41f0 20f8
  //   107c 83e 41f 20f 107 83 41 20 10 8 4 2 1 8*0 8000 c000 e000 f000 f800 fc00 fe00 ff00 ff80 ffc0 ffe0
  //   7ff0 3ff8 1ffc ffe 7ff 3ff 1ff ff 7f 3f 1f f 7 3 1 11*0 8000 4000 2000 1000 800 400 200 100 80 40 20
  //   10 8 4 2 1 9*0 8000 c000 e000 f000 f800 fc00 fe00 ff00 7f80 3fc0 1fe0 8ff0 47f8 23fc 11fe 8ff 47f
  //   23f 11f 8f 47 23 11 8 4 2 1 10*0 8000 4000 2000 1000 8800 4400 2200 1100 880 440 220 110 88 44 22 11
  //   8 4 2 1
  //   contents of rom_5 (hex, n*v repeats v):
  //   5*0 8000 4000 2000 1000 800 400 200 100 80 40 20 10 8 4 2 1 16*0 8000 4000 2000 1000 800 400 200 100
  //   8080 4040 2020 1010 808 404 202 101 80 40 20 10 8 4 2 1 102*0 8000 4000 2000 1000 800 8400 4200 a100
  //   5080 2840 1420 a10 8508 4284 2142 10a1 850 428 214 10a 85 42 21 10 8 4 2 1 4*0 8000 4000 2000 1000
  //   8800 4400 a200 d100 e880 f440 fa20 fd10 fe88 ff44 7fa2 3fd1 1fe8 ff4 7fa 3fd 1fe ff 7f 3f 1f f 7 3 1
  //   4*0 8000 4000 2000 1000 800 8400 4200 2100 1080 840 8420 4210 2108 1084 842 421 210 108 84 42 21 10
  //   8 4 2 1 11*0 8000 4000 2000 1000 800 400 200 100 80 40 20 10 8 4 2 1 15*0 8000 4000 a000 5000 2800
  //   9400 4a00 2500 1280 940 4a0 250 128 94 4a 25 12 9 4 2 1 6*0 8000 4000 2000 1000 8800 4400 2200 1100
  //   8880 4440 2220 1110 8888 4444 2222 1111 888 444 222 111 88 44 22 11 8 4 2 1
  //   contents of rom_6 (hex, n*v repeats v):
  //   5*0 8000 4000 2000 1000 800 8400 4200 2100 1080 840 420 210 108 84 42 21 10 8 4 2 1 11*0 8000 4000
  //   2000 1000 800 400 200 100 8080 4040 2020 1010 808 404 202 101 80 40 20 10 8 4 2 1 102*0 8000 4000
  //   2000 1000 800 8400 4200 a100 5080 2840 1420 a10 8508 4284 2142 10a1 850 428 214 10a 85 42 21 10 8 4
  //   2 1 4*0 8000 4000 2000 1000 8800 4400 2200 9100 4880 a440 5220 a910 5488 2a44 1522 a91 548 2a4 152
  //   a9 54 2a 15 a 5 2 1 6*0 8000 4000 2000 1000 800 8400 4200 2100 1080 840 8420 4210 2108 1084 842 421
  //   210 108 84 42 21 10 8 4 2 1 4*0 8000 c000 e000 f000 f800 fc00 fe00 ff00 ff80 ffc0 ffe0 fff0 fff8
  //   fffc fffe 7fff 3fff 1fff fff 7ff 3ff 1ff ff 7f 3f 1f f 7 3 1 8*0 8000 4000 a000 5000 2800 9400 ca00
  //   6500 3280 1940 ca0 650 328 194 ca 65 32 19 c 6 3 1 5*0 8000 4000 2000 1000 8800 4400 2200 1100 8880
  //   4440 2220 9110 4888 2444 1222 911 488 244 122 91 48 24 12 9 4 2 1
  //   contents of rom_7 (hex, n*v repeats v):
  //   6*0 8000 4000 2000 9000 4800 2400 1200 8900 c480 e240 f120 7890 3c48 1e24 f12 789 3c4 1e2 f1 78 3c
  //   1e f 7 3 1 5*0 8000 c000 e000 f000 f800 fc00 fe00 ff00 ff80 7fc0 3fe0 1ff0 ff8 7fc 3fe 1ff ff 7f 3f
  //   1f f 7 3 1 102*0 8000 4000 2000 1000 800 400 8200 c100 6080 3040 1820 c10 8608 4304 2182 10c1 860
  //   430 218 10c 86 43 21 10 8 4 2 1 4*0 8000 4000 2000 1000 8800 4400 a200 5100 2880 9440 4a20 2510 9288
  //   4944 24a2 1251 928 494 24a 125 92 49 24 12 9 4 2 1 5*0 8000 4000 2000 1000 800 8400 4200 2100 1080
  //   840 8420 4210 2108 1084 842 421 210 108 84 42 21 10 8 4 2 1 11*0 8000 4000 2000 1000 800 400 200 100
  //   80 40 20 10 8 4 2 1 15*0 8000 4000 2000 9000 4800 a400 d200 6900 3480 1a40 d20 690 348 1a4 d2 69 34
  //   1a d 6 3 1 6*0 8000 4000 2000 9000 4800 2400 1200 8900 4480 2240 9120 4890 2448 1224 912 489 244 122
  //   91 48 24 12 9 4 2 1
  //   contents of rom_8 (hex, n*v repeats v):
  //   6*0 8000 4000 a000 5000 2800 1400 a00 8500 4280 2140 10a0 850 428 214 10a 85 42 21 10 8 4 2 1 45*0
  //   8000 c000 e000 f000 f800 fc00 7e00 3f00 1f80 fc0 7e0 3f0 1f8 fc 7e 3f 1f f 7 3 1 11*0 8000 c000 e000
  //   f000 f800 fc00 7e00 3f00 1f80 fc0 7e0 3f0 1f8 fc 7e 3f 1f f 7 3 1 11*0 8000 c000 6000 b000 d800 ec00
  //   7600 3b00 1d80 ec0 760 3b0 1d8 ec 76 3b 1d e 7 3 1 4*0 8000 4000 2000 1000 8800 4400 2200 9100 4880
  //   2440 1220 910 8488 4244 2122 1091 848 424 212 109 84 42 21 10 8 4 2 1 4*0 8000 4000 2000 9000 4800
  //   a400 5200 2900 1480 8a40 4520 2290 1148 88a4 4452 2229 1114 88a 445 222 111 88 44 22 11 8 4 2 1 4*0
  //   8000 c000 e000 f000 f800 fc00 fe00 ff00 ff80 ffc0 ffe0 7ff0 3ff8 1ffc ffe 7ff 3ff 1ff ff 7f 3f 1f f
  //   7 3 1 11*0 8000 4000 2000 1000 800 400 200 100 80 40 20 10 8 4 2 1 11*0 8000 c000 e000 f000 f800
  //   7c00 3e00 1f00 f80 87c0 43e0 a1f0 50f8 287c 143e a1f 50f 287 143 a1 50 28 14 a 5 2 1 5*0 8000 4000
  //   2000 9000 4800 2400 1200 8900 4480 a240 5120 2890 1448 a24 512 289 144 a2 51 28 14 a 5 2 1
  //   contents of rom_9 (hex, n*v repeats v):
  //   7*0 8000 4000 2000 1000 800 400 8200 4100 2080 1040 820 410 208 104 82 41 20 10 8 4 2 1 5*0 8000
  //   c000 e000 f000 f800 fc00 fe00 ff00 ff80 ffc0 ffe0 fff0 fff8 fffc fffe 7fff 3fff 1fff fff 7ff 3ff 1ff
  //   ff 7f 3f 1f f 7 3 1 11*0 8000 4000 2000 1000 8800 4400 2200 1100 880 440 220 110 88 44 22 11 8 4 2 1
  //   12*0 8000 4000 2000 1000 8800 4400 2200 1100 880 440 220 110 88 44 22 11 8 4 2 1 12*0 8000 4000 2000
  //   9000 4800 2400 1200 900 480 240 120 90 48 24 12 9 4 2 1 5*0 8000 4000 2000 9000 4800 2400 1200 8900
  //   c480 e240 f120 f890 fc48 7e24 3f12 1f89 fc4 7e2 3f1 1f8 fc 7e 3f 1f f 7 3 1 5*0 8000 4000 a000 5000
  //   2800 1400 a00 500 280 8140 40a0 2050 1028 814 40a 205 102 81 40 20 10 8 4 2 1 7*0 8000 4000 2000
  //   1000 800 8400 4200 2100 1080 840 8420 4210 2108 1084 842 421 210 108 84 42 21 10 8 4 2 1 10*0 8000
  //   4000 a000 5000 2800 1400 a00 500 280 140 a0 50 28 14 a 5 2 1 14*0 8000 4000 2000 1000 800 8400 4200
  //   2100 9080 4840 2420 1210 908 484 242 121 90 48 24 12 9 4 2 1 5*0 8000 4000 a000 5000 2800 1400 8a00
  //   4500 a280 5140 28a0 1450 a28 514 28a 145 a2 51 28 14 a 5 2 1
  //   contents of rom_10 (hex, n*v repeats v):
  //   6*0 8000 4000 a000 5000 2800 1400 a00 8500 4280 2140 10a0 850 428 214 10a 85 42 21 10 8 4 2 1 12*0
  //   8000 4000 2000 1000 800 400 200 100 80 40 20 10 8 4 2 1 19*0 8000 4000 2000 1000 800 400 200 100 80
  //   40 20 10 8 4 2 1 16*0 8000 4000 2000 1000 800 400 200 100 80 40 20 10 8 4 2 1 16*0 8000 c000 6000
  //   3000 1800 c00 600 300 180 c0 60 30 18 c 6 3 1 6*0 8000 4000 2000 9000 4800 2400 1200 8900 4480 2240
  //   1120 890 8448 4224 2112 1089 844 422 211 108 84 42 21 10 8 4 2 1 5*0 8000 4000 a000 5000 2800 1400
  //   8a00 c500 e280 f140 f8a0 fc50 fe28 7f14 3f8a 1fc5 fe2 7f1 3f8 1fc fe 7f 3f 1f f 7 3 1 4*0 8000 4000
  //   2000 1000 800 8400 4200 2100 1080 840 8420 4210 2108 1084 842 421 210 108 84 42 21 10 8 4 2 1 10*0
  //   8000 4000 a000 5000 2800 1400 a00 500 280 140 a0 50 28 14 a 5 2 1 14*0 8000 4000 2000 1000 800 8400
  //   4200 2100 1080 840 420 210 108 84 42 21 10 8 4 2 1 9*0 8000 c000 6000 3000 1800 8c00 4600 a300 5180
  //   28c0 1460 a30 518 28c 146 a3 51 28 14 a 5 2 1
  //   contents of rom_11 (hex, n*v repeats v):
  //   5*0 8000 4000 2000 1000 8800 4400 2200 1100 8880 4440 2220 1110 888 444 222 111 88 44 22 11 8 4 2 1
  //   8*0 8000 4000 2000 1000 8800 4400 2200 1100 8880 4440 2220 1110 888 444 222 111 88 44 22 11 8 4 2 1
  //   16*0 8000 4000 2000 1000 800 400 200 100 80 40 20 10 8 4 2 1 16*0 8000 4000 2000 1000 800 400 200
  //   100 80 40 20 10 8 4 2 1 15*0 8000 c000 6000 3000 1800 c00 600 300 180 c0 60 30 18 c 6 3 1 6*0 8000
  //   4000 2000 1000 800 400 200 8100 4080 2040 1020 810 8408 4204 2102 1081 840 420 210 108 84 42 21 10 8
  //   4 2 1 6*0 8000 4000 2000 1000 800 8400 4200 2100 1080 8840 4420 2210 1108 884 442 221 110 88 44 22
  //   11 8 4 2 1 6*0 8000 4000 2000 1000 800 8400 4200 2100 1080 840 8420 4210 2108 1084 842 421 210 108
  //   84 42 21 10 8 4 2 1 9*0 8000 4000 2000 1000 8800 4400 2200 1100 880 440 220 110 88 44 22 11 8 4 2 1
  //   13*0 8000 4000 2000 1000 800 8400 4200 2100 1080 840 420 210 108 84 42 21 10 8 4 2 1 10*0 8000 4000
  //   2000 1000 8800 4400 2200 1100 880 440 220 110 88 44 22 11 8 4 2 1
  //   contents of rom_12 (hex, n*v repeats v):
  //   4*0 8000 4000 2000 1000 800 400 8200 4100 2080 9040 4820 2410 1208 904 482 241 120 90 48 24 12 9 4 2
  //   1 7*0 8000 c000 e000 f000 f800 fc00 7e00 3f00 1f80 8fc0 47e0 23f0 11f8 8fc 47e 23f 11f 8f 47 23 11 8
  //   4 2 1 16*0 8000 4000 2000 1000 800 400 200 100 80 40 20 10 8 4 2 1 16*0 8000 4000 2000 1000 800 400
  //   200 100 80 40 20 10 8 4 2 1 15*0 8000 c000 6000 3000 1800 c00 600 300 180 c0 60 30 18 c 6 3 1 6*0
  //   8000 4000 2000 1000 800 400 200 8100 4080 2040 1020 810 8408 4204 2102 1081 840 420 210 108 84 42 21
  //   10 8 4 2 1 6*0 8000 4000 2000 1000 800 8400 4200 2100 1080 840 8420 4210 2108 1084 842 421 210 108
  //   84 42 21 10 8 4 2 1 5*0 8000 c000 e000 f000 f800 fc00 fe00 ff00 ff80 ffc0 ffe0 7ff0 3ff8 1ffc ffe
  //   7ff 3ff 1ff ff 7f 3f 1f f 7 3 1 9*0 8000 4000 2000 1000 8800 4400 2200 1100 880 440 220 110 88 44 22
  //   11 8 4 2 1 8*0 8000 c000 e000 f000 f800 fc00 7e00 3f00 1f80 fc0 87e0 43f0 21f8 10fc 87e 43f 21f 10f
  //   87 43 21 10 8 4 2 1 10*0 8000 4000 2000 1000 8800 4400 2200 1100 880 440 220 110 88 44 22 11 8 4 2 1
  //   contents of rom_13 (hex, n*v repeats v):
  //   4*0 8000 4000 2000 1000 800 400 200 8100 4080 a040 5020 2810 1408 a04 502 281 140 a0 50 28 14 a 5 2
  //   1 12*0 8000 4000 2000 1000 8800 4400 2200 1100 880 440 220 110 88 44 22 11 8 4 2 1 13*0 8000 4000
  //   2000 1000 8800 4400 2200 1100 880 440 220 110 88 44 22 11 8 4 2 1 12*0 8000 4000 2000 1000 8800 4400
  //   2200 1100 880 440 220 110 88 44 22 11 8 4 2 1 13*0 8000 4000 2000 9000 4800 2400 1200 900 480 240
  //   120 90 48 24 12 9 4 2 1 5*0 8000 4000 2000 1000 800 400 200 8100 4080 2040 1020 810 8408 4204 2102
  //   1081 840 420 210 108 84 42 21 10 8 4 2 1 5*0 8000 4000 a000 5000 2800 1400 a00 8500 4280 2140 90a0
  //   c850 6428 3214 190a c85 642 321 190 c8 64 32 19 c 6 3 1 0 0 0 8000 4000 a000 5000 2800 1400 a00 8500
  //   4280 2140 10a0 850 8428 4214 210a 1085 842 421 210 108 84 42 21 10 8 4 2 1 8*0 8000 4000 2000 1000
  //   800 400 8200 4100 2080 1040 820 410 208 104 82 41 20 10 8 4 2 1 12*0 8000 4000 2000 1000 800 8400
  //   4200 2100 1080 840 420 210 108 84 42 21 10 8 4 2 1 10*0 8000 4000 2000 1000 8800 4400 2200 1100 880
  //   440 220 110 88 44 22 11 8 4 2 1
  //   contents of rom_14 (hex, n*v repeats v):
  //   12*0 8000 4000 a000 5000 2800 1400 a00 500 280 140 a0 50 28 14 a 5 2 1 11*0 8000 4000 2000 9000 4800
  //   a400 5200 2900 1480 a40 520 290 148 a4 52 29 14 a 5 2 1 12*0 8000 c000 e000 f000 f800 fc00 7e00 3f00
  //   1f80 fc0 7e0 3f0 1f8 fc 7e 3f 1f f 7 3 1 11*0 8000 c000 e000 f000 f800 fc00 7e00 3f00 1f80 fc0 7e0
  //   3f0 1f8 fc 7e 3f 1f f 7 3 1 11*0 8000 c000 e000 7000 b800 dc00 6e00 3700 1b80 dc0 6e0 370 1b8 dc 6e
  //   37 1b d 6 3 1 4*0 8000 4000 2000 1000 800 400 200 8100 c080 e040 f020 f810 fc08 7e04 3f02 1f81 fc0
  //   7e0 3f0 1f8 fc 7e 3f 1f f 7 3 1 5*0 8000 4000 a000 5000 2800 1400 a00 500 8280 c140 60a0 3050 1828
  //   c14 60a 305 182 c1 60 30 18 c 6 3 1 5*0 8000 4000 2000 1000 800 400 200 8100 4080 2040 1020 810 408
  //   204 102 81 40 20 10 8 4 2 1 12*0 8000 4000 2000 1000 800 400 200 100 8080 4040 2020 1010 808 404 202
  //   101 80 40 20 10 8 4 2 1 11*0 8000 4000 2000 1000 800 8400 4200 2100 1080 840 420 210 108 84 42 21 10
  //   8 4 2 1 10*0 8000 4000 2000 1000 8800 4400 2200 1100 880 440 220 110 88 44 22 11 8 4 2 1
  //   contents of rom_15 (hex, n*v repeats v):
  //   0 0 8000 c000 e000 f000 f800 fc00 fe00 ff00 ff80 ffc0 7fe0 3ff0 1ff8 8ffc 47fe 23ff 11ff 8ff 47f 23f
  //   11f 8f 47 23 11 8 4 2 1 10*0 8000 4000 a000 5000 2800 1400 8a00 4500 2280 1140 8a0 450 228 114 8a 45
  //   22 11 8 4 2 1 101*0 8000 4000 a000 5000 2800 1400 8a00 4500 2280 1140 8a0 8450 4228 2114 108a 845
  //   422 211 108 84 42 21 10 8 4 2 1 4*0 8000 4000 2000 1000 8800 4400 2200 1100 8880 4440 a220 d110 6888
  //   3444 1a22 d11 688 344 1a2 d1 68 34 1a d 6 3 1 4*0 8000 4000 2000 1000 800 400 200 8100 4080 2040
  //   1020 810 408 204 102 81 40 20 10 8 4 2 1 11*0 8000 4000 2000 1000 800 400 200 100 80 40 8020 4010
  //   2008 1004 802 401 200 100 80 40 20 10 8 4 2 1 10*0 8000 4000 2000 1000 800 8400 4200 2100 1080 840
  //   420 210 108 84 42 21 10 8 4 2 1 5*0 8000 c000 e000 f000 f800 fc00 fe00 ff00 ff80 ffc0 ffe0 fff0 fff8
  //   fffc fffe 7fff 3fff 1fff fff 7ff 3ff 1ff ff 7f 3f 1f f 7 3 1
  //   contents of rom_16 (hex, n*v repeats v):
  //   34*0 8000 c000 e000 f000 f800 fc00 fe00 ff00 ff80 7fc0 3fe0 1ff0 ff8 7fc 83fe 41ff 20ff 107f 83f 41f
  //   20f 107 83 41 20 10 8 4 2 1 101*0 8000 4000 2000 1000 800 400 200 100 80 40 20 10 8 4 2 1 13*0 8000
  //   4000 2000 1000 800 400 8200 4100 a080 5040 2820 1410 a08 8504 c282 6141 30a0 1850 c28 614 30a 185 c2
  //   61 30 18 c 6 3 1 0 0 8000 c000 e000 f000 f800 fc00 fe00 7f00 3f80 1fc0 fe0 7f0 3f8 1fc fe 7f 3f 1f f
  //   7 3 1 10*0 8000 c000 6000 3000 1800 c00 600 300 180 c0 60 30 18 800c c006 6003 3001 1800 c00 600 300
  //   180 c0 60 30 18 c 6 3 1 8*0 8000 4000 2000 1000 800 8400 4200 2100 1080 840 420 210 108 84 42 21 10
  //   8 4 2 1
  //   contents of rom_17 (hex, n*v repeats v):
  //   24*0 8000 4000 2000 1000 800 400 200 100 80 40 20 10 8 4 2 1 13*0 8000 c000 e000 f000 f800 fc00 fe00
  //   ff00 ff80 7fc0 3fe0 1ff0 ff8 7fc 3fe 1ff ff 7f 3f 1f f 7 3 1 106*0 8000 4000 2000 1000 800 400 8200
  //   4100 2080 1040 820 410 208 104 82 41 20 10 8 4 2 1 9*0 8000 4000 2000 1000 800 400 8200 4100 2080
  //   1040 820 410 208 104 82 41 20 10 8 4 2 1 13*0 8000 4000 2000 1000 800 400 200 100 80 40 20 10 8 4 2
  //   1 16*0 8000 4000 2000 1000 800 400 200 100 80 40 20 10 8 4 2 1 16*0 8000 4000 2000 9000 4800 2400
  //   1200 900 480 240 120 90 48 24 12 9 4 2 1 11*0 8000 4000 2000 1000 8800 4400 2200 1100 880 440 220
  //   110 88 44 22 11 8 4 2 1
  //   contents of rom_18 (hex, n*v repeats v):
  //   23*0 8000 4000 2000 1000 800 400 200 8100 4080 2040 1020 810 408 204 102 81 40 20 10 8 4 2 1 7*0
  //   8000 4000 2000 1000 800 400 200 100 8080 4040 2020 1010 808 404 202 101 80 40 20 10 8 4 2 1 106*0
  //   8000 4000 2000 1000 800 400 8200 4100 2080 1040 820 410 208 104 82 41 20 10 8 4 2 1 9*0 8000 4000
  //   2000 9000 4800 2400 9200 4900 2480 9240 4920 2490 1248 924 492 249 124 92 49 24 12 9 4 2 1 10*0 8000
  //   4000 2000 1000 800 400 200 100 80 40 20 10 8 4 2 1 16*0 8000 4000 2000 1000 800 400 200 100 80 40 20
  //   10 8 4 2 1 16*0 8000 4000 2000 9000 4800 2400 1200 900 480 240 120 90 48 24 12 9 4 2 1 11*0 8000
  //   4000 2000 1000 8800 4400 2200 1100 880 440 220 110 88 44 22 11 8 4 2 1
  //   contents of rom_19 (hex, n*v repeats v):
  //   23*0 8000 4000 2000 1000 800 400 8200 4100 2080 1040 820 410 208 104 82 41 20 10 8 4 2 1 8*0 8000
  //   4000 2000 1000 800 400 200 100 8080 4040 2020 1010 808 404 202 101 80 40 20 10 8 4 2 1 106*0 8000
  //   4000 2000 1000 800 400 200 8100 4080 2040 1020 810 408 204 102 81 40 20 10 8 4 2 1 8*0 8000 4000
  //   2000 1000 8800 4400 a200 5100 a880 5440 2a20 1510 a88 544 2a2 151 a8 54 2a 15 a 5 2 1 11*0 8000 4000
  //   2000 1000 800 400 200 100 80 40 20 10 8 4 2 1 16*0 8000 4000 2000 1000 800 400 200 100 80 40 20 10 8
  //   4 2 1 16*0 8000 4000 2000 9000 4800 2400 1200 900 480 240 120 90 48 24 12 9 4 2 1 11*0 8000 4000
  //   2000 1000 8800 4400 2200 1100 880 440 220 110 88 44 22 11 8 4 2 1
  //   contents of rom_20 (hex, n*v repeats v):
  //   19*0 8000 c000 e000 f000 f800 fc00 fe00 ff00 ff80 7fc0 bfe0 5ff0 2ff8 17fc bfe 5ff 2ff 17f bf 5f 2f
  //   17 b 5 2 1 8*0 8000 c000 e000 f000 f800 fc00 fe00 ff00 ff80 7fc0 3fe0 1ff0 ff8 7fc 3fe 1ff ff 7f 3f
  //   1f f 7 3 1 102*0 8000 c000 e000 f000 f800 7c00 3e00 9f00 cf80 e7c0 f3e0 f9f0 fcf8 7e7c 3f3e 1f9f fcf
  //   7e7 3f3 1f9 fc 7e 3f 1f f 7 3 1 0 0 0 8000 c000 e000 f000 f800 7c00 3e00 1f00 f80 7c0 83e0 41f0 20f8
  //   107c 83e 41f 20f 107 83 41 20 10 8 4 2 1 8*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
  //   contents of rom_21 (hex, n*v repeats v):
  //   21*0 8000 4000 2000 1000 800 400 200 100 80 40 20 10 8 4 2 1 16*0 8000 4000 2000 1000 800 400 200
  //   100 8080 4040 2020 1010 808 404 202 101 80 40 20 10 8 4 2 1 102*0 8000 4000 2000 1000 800 8400 4200
  //   a100 5080 2840 1420 a10 8508 4284 2142 10a1 850 428 214 10a 85 42 21 10 8 4 2 1 4*0 8000 4000 2000
  //   100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
  //   contents of rom_22 (hex, n*v repeats v):
  //   21*0 8000 4000 2000 1000 800 8400 4200 2100 1080 840 420 210 108 84 42 21 10 8 4 2 1 11*0 8000 4000
  //   2000 1000 800 400 200 100 8080 4040 2020 1010 808 404 202 101 80 40 20 10 8 4 2 1 102*0 8000 4000
  //   2000 1000 800 8400 4200 a100 5080 2840 1420 a10 8508 4284 2142 10a1 850 428 214 10a 85 42 21 10 8 4
  //   2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
  //   contents of rom_23 (hex, n*v repeats v):
  //   22*0 8000 4000 2000 9000 4800 2400 1200 8900 c480 e240 f120 7890 3c48 1e24 f12 789 3c4 1e2 f1 78 3c
  //   1e f 7 3 1 5*0 8000 c000 e000 f000 f800 fc00 fe00 ff00 ff80 7fc0 3fe0 1ff0 ff8 7fc 3fe 1ff ff 7f 3f
  //   1f f 7 3 1 102*0 8000 4000 2000 1000 800 400 8200 c100 6080 3040 1820 c10 8608 4304 2182 10c1 860 43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
  //   contents of rom_24 (hex, n*v repeats v):
  //   22*0 8000 4000 a000 5000 2800 1400 a00 8500 4280 2140 10a0 850 428 214 10a 85 42 21 10 8 4 2 1 45*0
  //   8000 c000 e000 f000 f800 fc00 7e00 3f00 1f80 fc0 7e0 3f0 1f8 fc 7e 3f 1f f 7 3 1 11*0 8000 c000 e000
  //   f000 f800 fc00 7e00 3f00 1f80 fc0 7e0 3f0 1f8 fc 7e 3f 1f f 7 3 1 11*0 8000 c000 6000 b000 d800 ec0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
  //   contents of rom_25 (hex, n*v repeats v):
  //   23*0 8000 4000 2000 1000 800 400 8200 4100 2080 1040 820 410 208 104 82 41 20 10 8 4 2 1 5*0 8000
  //   c000 e000 f000 f800 fc00 fe00 ff00 ff80 ffc0 ffe0 fff0 fff8 fffc fffe 7fff 3fff 1fff fff 7ff 3ff 1ff
  //   ff 7f 3f 1f f 7 3 1 11*0 8000 4000 2000 1000 8800 4400 2200 1100 880 440 220 110 88 44 22 11 8 4 2 1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
  //   contents of rom_26 (hex, n*v repeats v):
  //   22*0 8000 4000 a000 5000 2800 1400 a00 8500 4280 2140 10a0 850 428 214 10a 85 42 21 10 8 4 2 1 12*0
  //   8000 4000 2000 1000 800 400 200 100 80 40 20 10 8 4 2 1 19*0 8000 4000 2000 1000 800 400 200 100 80
  //   40 20 10 8 4 2 1 16*0 8000 4000 2000 1000 800 400 200 100 80 40 20 10 8 4 2 1 16*0 8000 c000 6000 30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
  //   contents of rom_27 (hex, n*v repeats v):
  //   21*0 8000 4000 2000 1000 8800 4400 2200 1100 8880 4440 2220 1110 888 444 222 111 88 44 22 11 8 4 2 1
  //   8*0 8000 4000 2000 1000 8800 4400 2200 1100 8880 4440 2220 1110 888 444 222 111 88 44 22 11 8 4 2 1
  //   16*0 8000 4000 2000 1000 800 400 200 100 80 40 20 10 8 4 2 1 16*0 8000 4000 2000 1000 800 400 200 1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
  //   contents of rom_28 (hex, n*v repeats v):
  //   20*0 8000 4000 2000 1000 800 400 8200 4100 2080 9040 4820 2410 1208 904 482 241 120 90 48 24 12 9 4
  //   2 1 7*0 8000 c000 e000 f000 f800 fc00 7e00 3f00 1f80 8fc0 47e0 23f0 11f8 8fc 47e 23f 11f 8f 47 23 11
  //   8 4 2 1 16*0 8000 4000 2000 1000 800 400 200 100 80 40 20 10 8 4 2 1 16*0 8000 4000 2000 1000 800 4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
  //   contents of rom_29 (hex, n*v repeats v):
  //   20*0 8000 4000 2000 1000 800 400 200 8100 4080 a040 5020 2810 1408 a04 502 281 140 a0 50 28 14 a 5 2
  //   1 12*0 8000 4000 2000 1000 8800 4400 2200 1100 880 440 220 110 88 44 22 11 8 4 2 1 13*0 8000 4000
  //   2000 1000 8800 4400 2200 1100 880 440 220 110 88 44 22 11 8 4 2 1 12*0 8000 4000 2000 1000 8800 4400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
  //   contents of rom_30 (hex, n*v repeats v):
  //   28*0 8000 4000 a000 5000 2800 1400 a00 500 280 140 a0 50 28 14 a 5 2 1 11*0 8000 4000 2000 9000 4800
  //   a400 5200 2900 1480 a40 520 290 148 a4 52 29 14 a 5 2 1 12*0 8000 c000 e000 f000 f800 fc00 7e00 3f00
  //   1f80 fc0 7e0 3f0 1f8 fc 7e 3f 1f f 7 3 1 11*0 8000 c000 e000 f000 f800 fc00 7e00 3f00 1f80 fc0 7e0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
  //   contents of rom_31 (hex, n*v repeats v):
  //   18*0 8000 c000 e000 f000 f800 fc00 fe00 ff00 ff80 ffc0 7fe0 3ff0 1ff8 8ffc 47fe 23ff 11ff 8ff 47f
  //   23f 11f 8f 47 23 11 8 4 2 1 10*0 8000 4000 a000 5000 2800 1400 8a00 4500 2280 1140 8a0 450 228 114
  //   8a 45 22 11 8 4 2 1 101*0 8000 4000 a000 5000 2800 1400 8a00 4500 2280 1140 8a0 8450 4228 2114 108a
  //   845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
  //   contents of rom_32 (hex, n*v repeats v):
  //   50*0 8000 c000 e000 f000 f800 fc00 fe00 ff00 ff80 7fc0 3fe0 1ff0 ff8 7fc 83fe 41ff 20ff 107f 83f 41f
  //   20f 107 83 41 20 10 8 4 2 1 101*0 8000 4000 2000 1000 800 400 200 100 80 40 20 10 8 4 2 1 13*0 8000
  //   4000 2000 1000 800 400 8200 4100 a080 5040 2820 1410 a08 8504 c282 6141 30a0 1850 c28 614 30a 185 c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
endmodule

module \_0_f计数器  (
  output [8:0] out_1
);

  wire button_1_out, clock_1_out;
  wire [8:0] adder_1_out;

  Adder #(.width(9)) adder_1 (.a(out_1), .b({9{1'b0}}), .out(adder_1_out), .cin(1'b1));  // open: cout
  Register #(.width(9)) register_1 (.D(adder_1_out), .en(1'b1), .Q(out_1), .clk(clock_1_out), .clr(button_1_out));
  Clock clock_1 (.out(clock_1_out));
  Button button_1 (.out(button_1_out));
endmodule
