// Logisim project led+滚动.circ as structural Verilog: 2 circuits, main circuit main
module main (
);

  wire [8:0] \n0_f计数器_1_out_1 ;
  wire [15:0] rom_1_data, rom_2_data, rom_3_data, rom_4_data, rom_5_data, rom_6_data, rom_7_data, rom_8_data,
       rom_9_data, rom_10_data, rom_11_data, rom_12_data, rom_13_data, rom_14_data, rom_15_data, rom_16_data;

  \_0_f计数器  \u_0_f计数器_1  (.out_1(\n0_f计数器_1_out_1 ));
  ROM #(.addrWidth(9), .dataWidth(16)) rom_1 (.addr(\n0_f计数器_1_out_1 ), .data(rom_1_data));  // open: sel
  ROM #(.addrWidth(9), .dataWidth(16)) rom_2 (.addr(\n0_f计数器_1_out_1 ), .data(rom_2_data));  // open: sel
  ROM #(.addrWidth(9), .dataWidth(16)) rom_3 (.addr(\n0_f计数器_1_out_1 ), .data(rom_3_data));  // open: sel
  ROM #(.addrWidth(9), .dataWidth(16)) rom_4 (.addr(\n0_f计数器_1_out_1 ), .data(rom_4_data));  // open: sel
  ROM #(.addrWidth(9), .dataWidth(16)) rom_5 (.addr(\n0_f计数器_1_out_1 ), .data(rom_5_data));  // open: sel
  ROM #(.addrWidth(9), .dataWidth(16)) rom_6 (.addr(\n0_f计数器_1_out_1 ), .data(rom_6_data));  // open: sel
  ROM #(.addrWidth(9), .dataWidth(16)) rom_7 (.addr(\n0_f计数器_1_out_1 ), .data(rom_7_data));  // open: sel
  ROM #(.addrWidth(9), .dataWidth(16)) rom_8 (.addr(\n0_f计数器_1_out_1 ), .data(rom_8_data));  // open: sel
  ROM #(.addrWidth(9), .dataWidth(16)) rom_9 (.addr(\n0_f计数器_1_out_1 ), .data(rom_9_data));  // open: sel
  ROM #(.addrWidth(9), .dataWidth(16)) rom_10 (.addr(\n0_f计数器_1_out_1 ), .data(rom_10_data));  // open: sel
  ROM #(.addrWidth(9), .dataWidth(16)) rom_11 (.addr(\n0_f计数器_1_out_1 ), .data(rom_11_data));  // open: sel
  ROM #(.addrWidth(9), .dataWidth(16)) rom_12 (.addr(\n0_f计数器_1_out_1 ), .data(rom_12_data));  // open: sel
  ROM #(.addrWidth(9), .dataWidth(16)) rom_13 (.addr(\n0_f计数器_1_out_1 ), .data(rom_13_data));  // open: sel
  ROM #(.addrWidth(9), .dataWidth(16)) rom_14 (.addr(\n0_f计数器_1_out_1 ), .data(rom_14_data));  // open: sel
  ROM #(.addrWidth(9), .dataWidth(16)) rom_15 (.addr(\n0_f计数器_1_out_1 ), .data(rom_15_data));  // open: sel
  ROM #(.addrWidth(9), .dataWidth(16)) rom_16 (.addr(\n0_f计数器_1_out_1 ), .data(rom_16_data));  // open: sel
  DotMatrix #(.inputtype("row"), .matrixcols(16), .matrixrows(16)) dotmatrix_1 (
    .row0(rom_1_data), .row1(rom_2_data), .row2(rom_3_data), .row3(rom_4_data), .row4(rom_5_data),
    .row5(rom_6_data), .row6(rom_7_data), .row7(rom_8_data), .row8(rom_9_data), .row9(rom_10_data),
    .row10(rom_11_data), .row11(rom_12_data), .row12(rom_13_data), .row13(rom_14_data), .row14(rom_15_data),
    .row15(rom_16_data));

  // Notes on the sheet:
  //   1
  //   2
  //   3
  //   4
  //   5
  //   6
  //   7
  //   8
  //   9
  //   10
  //   11
  //   12
  //   13
  //   14
  //   15
  //   16
  //   contents of rom_1 (hex, n*v repeats v):
  //   800000 400000 200000 100000 80000 40000 20000 10000  8000 4000 2000 1000 800 400 200 100  80 40 20
  //   10 8 4 2 1  0 0 0 0 0 0 0 0  0 0 0 0 0 0 0 0  0 0 0 0 0 0 0 0  0 0 0 0 0 0 0 0  0 0 0 0 0 0 0 0
  //   1ff00000 ff80000 7fc0000 3fe0000 1ff0000 ff8000 7fc000 3fe000 1ff000 ff800 7fc00 3fe00 1ff00 ff80
  //   7fc0 3fe0 1ff0 ff8 7fc 3fe 1ff ff 7f 3f 1f f 7 3 1 0 0 0 10200000 8100000 4080000 2040000 1020000
  //   810000 408000 204000 102000 81000 40800 20400 10200 8100 4080 2040 1020 810 408 204 102 81 40 20 10
  //   8 4 2 1 0 0 0  200000 100000 80000 40000 20000 10000 8000 4000 2000 1000 800 400 200 100 80 40 20 10
  //   8 4 2 1 0 0 0 0 0 0 0 0 0 0 0 0 0 0 0 0 0 0 0 0 0 0 0 0 0 0 0 0 0 0 0 0 0 0 0 0 0 0 0 0 0 0 80000
  //   40000 20000 10000 8000 4000 2000 1000 800 400 200 100 80 40 20 10 8 4 2 1 0 0 0 0 0 0 0 0 0 0 0 0
  //   10400000 8200000 4100000 2080000 1040000 820000 410000 208000 104000 82000 41000 20800 10400 8200
  //   4100 2080 1040 820 410 208 104 82 41 20 10 8 4 2 1 0 0 0  0 0 0 0 0 0 0 0 0 0 0 0 0 0 0 0 0 0 0 0 0
  //   0 0 0 0 0 0 0 0 0 0 0 0 0 0 0 0 0 0 0 0 0 0 0 0 0 0 0 0 0 0 0 0 0 0 0 0 0 0 0 0 0 0 0 47b10000
  //   a3d88000 d1ec4000 68f62000 347b1000 9a3d8800 cd1ec400 668f6200 3347b100 99a3d880 ccd1ec40 6668f620
  //   b3347b10 599a3d88 2ccd1ec4 16668f62 8b3347b1 c599a3d9 e2ccd1ed f16668f7 f8b3347c fc599a3e fe2ccd1f
  //   ff166690 ff8b3348 ffc599a4 ffe2ccd2 fff16669 fff8b335 fffc599b fffe2cce ffff1667 7ffb0000 3ffd8000
  //   1ffec000 fff6000 7ffb000 3ffd800 1ffec00 fff600 7ffb00 3ffd80 1ffec0 fff60 7ffb0 3ffd8 1ffec fff6
  //   7ffb 3ffd 1ffe fff 7ff 3ff 1ff ff 7f 3f 1f f 7 3 1 0 fd400000 fea00000 7f500000 3fa80000 1fd40000
  //   8fea0000 47f50000 a3fa8000 d1fd4000 e8fea000 f47f5000 fa3fa800 fd1fd400 7e8fea00 bf47f500 dfa3fa80
  //   6fd1fd40 37e8fea0 1bf47f50 dfa3fa8 6fd1fd4 37e8fea 1bf47f5 dfa3fa 6fd1fd 37e8fe 1bf47f dfa3f 6fd1f
  //   37e8f 1bf47 dfa3 0 0 0 0 0 0 0 0 0 0 0 0 0 0 0 0 0 0 0 0 0 0 0 0 0 0 0 0 0 0 0 0 0 0 0 0 0 0 0 0 0 0
  //   0 0 0 0 0 0 0 0 0 0 0 0 0 0 0 0 0 0 0 0 0 0  0 0 0 0 0 0 0 0 0 0 0 0 0 0 0 0 0 0 0 0 0 0 0 0 0 0 0 0
  //   0 0 0 0
  //   contents of rom_2 (hex, n*v repeats v):
  //   20400000 10200000 8100000 4080000 2040000 1020000 810000 408000 204000 102000 81000 40800 20400
  //   10200 8100 4080 2040 1020 810 408 204 102 81 40 20 10 8 4 2 1 0 0 3ff80000 1ffc0000 ffe0000 7ff0000
  //   3ff8000 1ffc000 ffe000 7ff000 3ff800 1ffc00 ffe00 7ff00 3ff80 1ffc0 ffe0 7ff0 3ff8 1ffc ffe 7ff 3ff
  //   1ff ff 7f 3f 1f f 7 3 1 0 0 10100000 8080000 4040000 2020000 1010000 808000 404000 202000 101000
  //   80800 40400 20200 10100 8080 4040 2020 1010 808 404 202 101 80 40 20  10 8 4 2 1 0 0 0 10200000
  //   8100000 4080000 2040000 1020000 810000 408000 204000 102000 81000 40800 20400 10200 8100 4080 2040
  //   1020 810 408 204 102 81 40 20 10 8 4 2 1 0 0 0 400000 200000 100000 80000 40000 20000 10000 8000
  //   4000 2000 1000 800 400 200 100 80 40 20 10 8 4 2 1 0 0 0 0 0 0 0 0 0 7ffe0000 3fff0000 1fff8000
  //   fffc000 7ffe000 3fff000 1fff800 fffc00 7ffe00 3fff00 1fff80 fffc0 7ffe0 3fff0 1fff8 fffc 7ffe 3fff
  //   1fff fff 7ff 3ff 1ff ff 7f 3f 1f f 7 3 1 0 1fc0000 fe0000 7f0000 3f8000 1fc000 fe000 7f000 3f800
  //   1fc00 fe00 7f00 3f80 1fc0 fe0 7f0 3f8 1fc fe 7f 3f 1f f 7 3 1 0 0 0 0 0 0 0  10400000 8200000
  //   4100000 2080000 1040000 820000 410000 208000 104000 82000 41000 20800 10400 8200 4100 2080 1040 820
  //   410 208 104 82 41 20 10 8 4 2 1 0 0 0 0 0 0 0 0 0 0 0 0 0 0 0 0 0 0 0 0 0 0 0 0 0 0 0 0 0 0 0 0 0 0
  //   0 0 0 0 0 0 0 0 0 0 0 0 0 0 0 0 0 0 0 0 0 0 0 0 0 0 0 0 0 0 0 0 0 47b10000 a3d88000 d1ec4000
  //   68f62000 347b1000 9a3d8800 cd1ec400 668f6200 3347b100 99a3d880 ccd1ec40 6668f620 b3347b10 599a3d88
  //   2ccd1ec4 16668f62 8b3347b1 c599a3d9 e2ccd1ed f16668f7 f8b3347c fc599a3e fe2ccd1f ff166690 ff8b3348
  //   ffc599a4 ffe2ccd2 fff16669 fff8b335 fffc599b fffe2cce ffff1667 7ffb0000 3ffd8000 1ffec000 fff6000
  //   7ffb000 3ffd800 1ffec00 fff600 7ffb00 3ffd80 1ffec0 fff60 7ffb0 3ffd8 1ffec fff6  7ffb 3ffd 1ffe fff
  //   7ff 3ff 1ff ff 7f 3f 1f f 7 3 1 0 fd400000 fea00000 7f500000 3fa80000 1fd40000 8fea0000 47f50000
  //   a3fa8000 d1fd4000 e8fea000 f47f5000 fa3fa800 fd1fd400 7e8fea00 bf47f500 dfa3fa80 6fd1fd40 37e8fea0
  //   1bf47f50 dfa3fa8 6fd1fd4 37e8fea 1bf47f5 dfa3fa 6fd1fd 37e8fe 1bf47f dfa3f 6fd1f 37e8f 1bf47 dfa3 0
  //   0 0 0 0 0 0 0 0 0 0 0 0 0 0 0 0 0 0 0 0 0 0 0 0 0 0 0 0 0 0 0 0 0 0 0 0 0 0 0 0 0 0 0 0 0 0 0 0 0 0
  //   0 0 0 0 0 0 0 0 0 0 0 0 0 0 0 0 0 0 0 0 0 0 0 0 0 0 0 0 0 0 0 0 0 0 0 0 0  0 0 0 0 0 0 0 0
  //   contents of rom_3 (hex, n*v repeats v):
  //   10400000 8200000 4100000 2080000 1040000 820000 410000 208000 104000 82000 41000 20800 10400 8200
  //   4100 2080 1040 820 410 208 104 82 41 20 10 8 4 2 1 0 0 0 21080000 10840000 8420000 4210000 2108000
  //   1084000 842000 421000 210800 108400 84200 42100 21080 10840 8420 4210 2108 1084 842 421 210 108 84
  //   42 21 10 8 4 2 1 0 0 10100000 8080000 4040000 2020000 1010000 808000 404000 202000 101000 80800
  //   40400 20200 10100 8080 4040 2020 1010 808 404 202 101 80 40 20 10 8 4 2 1 0 0 0 10200000 8100000
  //   4080000 2040000 1020000 810000 408000 204000 102000 81000 40800 20400 10200 8100 4080 2040 1020 810
  //   408 204 102 81 40 20  10 8 4 2 1 0 0 0 fc0000 7e0000 3f0000 1f8000 fc000 7e000 3f000 1f800 fc00 7e00
  //   3f00 1f80 fc0 7e0 3f0 1f8 fc 7e 3f 1f f 7 3 1 0 0 0 0 0 0 0 0 100000 80000 40000 20000 10000 8000
  //   4000 2000 1000 800 400 200 100 80 40 20 10 8 4 2 1 0 0 0 0 0 0 0 0 0 0 0 7e100000 3f080000 1f840000
  //   fc20000 7e10000 3f08000 1f84000 fc2000 7e1000 3f0800 1f8400 fc200 7e100 3f080 1f840 fc20 7e10 3f08
  //   1f84 fc2 7e1 3f0 1f8 fc 7e 3f 1f f 7 3 1 0 20400000 10200000 8100000 4080000 2040000 1020000 810000
  //   408000 204000 102000 81000 40800 20400 10200 8100 4080 2040 1020 810 408 204 102 81 40  20 10 8 4 2
  //   1 0 0 0 0 0 0 0 0 0 0 0 0 0 0 0 0 0 0 0 0 0 0 0 0 0 0 0 0 0 0 0 0 0 0 0 0 0 0 0 0 0 0 0 0 0 0 0 0 0
  //   0 0 0 0 0 0 0 0 0 0 0 0 0 0 0 0 0 47b10000 a3d88000 d1ec4000 68f62000 347b1000 9a3d8800 cd1ec400
  //   668f6200 3347b100 99a3d880 ccd1ec40 6668f620 b3347b10 599a3d88 2ccd1ec4 16668f62 8b3347b1 c599a3d9
  //   e2ccd1ed f16668f7 f8b3347c fc599a3e fe2ccd1f ff166690 ff8b3348 ffc599a4 ffe2ccd2 fff16669 fff8b335
  //   fffc599b fffe2cce ffff1667 7ffb0000 3ffd8000 1ffec000 fff6000 7ffb000 3ffd800 1ffec00 fff600 7ffb00
  //   3ffd80 1ffec0 fff60 7ffb0 3ffd8 1ffec fff6 7ffb 3ffd 1ffe fff 7ff 3ff 1ff ff 7f 3f 1f f 7 3 1 0
  //   fd400000 fea00000 7f500000 3fa80000 1fd40000 8fea0000 47f50000 a3fa8000  d1fd4000 e8fea000 f47f5000
  //   fa3fa800 fd1fd400 7e8fea00 bf47f500 dfa3fa80 6fd1fd40 37e8fea0 1bf47f50 dfa3fa8 6fd1fd4 37e8fea
  //   1bf47f5 dfa3fa 6fd1fd 37e8fe 1bf47f dfa3f 6fd1f 37e8f 1bf47 dfa3 0 0 0 0 0 0 0 0 0 0 0 0 0 0 0 0 0 0
  //   0 0 0 0 0 0 0 0 0 0 0 0 0 0 0 0 0 0 0 0 0 0 0 0 0 0 0 0 0 0 0 0 0 0 0 0 0 0 0 0 0 0 0 0 0 0 0 0 0 0
  //   0 0 0 0 0 0 0 0 0 0 0 0 0 0 0 0 0 0 0 0 0 0 0 0 0 0 0 0
  //   contents of rom_4 (hex, n*v repeats v):
  //   17fc0000 bfe0000 5ff0000 2ff8000 17fc000 bfe000 5ff000 2ff800 17fc00 bfe00 5ff00 2ff80 17fc0 bfe0
  //   5ff0 2ff8 17fc bfe 5ff 2ff 17f bf 5f 2f  17 b 5 2 1 0 0 0 21080000 10840000 8420000 4210000 2108000
  //   1084000 842000 421000 210800 108400 84200 42100 21080 10840 8420 4210 2108 1084 842 421 210 108 84
  //   42 21 10 8 4 2 1 0 0 1ff00000 ff80000 7fc0000 3fe0000 1ff0000 ff8000 7fc000 3fe000 1ff000 ff800
  //   7fc00 3fe00 1ff00 ff80 7fc0 3fe0 1ff0 ff8 7fc 3fe 1ff ff 7f 3f 1f f 7 3 1 0 0 0 10a80000 8540000
  //   42a0000 2150000 10a8000 854000 42a000 215000 10a800 85400 42a00 21500 10a80 8540 42a0 2150 10a8 854
  //   42a 215 10a 85 42 21 10 8 4 2 1 0 0 0 fc840000 7e420000 3f210000 1f908000 fc84000 7e42000 3f21000
  //   1f90800 fc8400 7e4200 3f2100 1f9080 fc840 7e420 3f210 1f908  fc84 7e42 3f21 1f90 fc8 7e4 3f2 1f9 fc
  //   7e 3f 1f f 7 3 1 100000 80000 40000 20000 10000 8000 4000 2000 1000 800 400 200 100 80 40 20 10 8 4
  //   2 1 0 0 0 0 0 0 0 0 0 0 0 22100000 11080000 8840000 4420000 2210000 1108000 884000 442000 221000
  //   110800 88400 44200 22100 11080 8840 4420 2210 1108 884 442 221 110 88 44 22 11 8 4 2 1 0 0 7e7c0000
  //   3f3e0000 1f9f0000 fcf8000 7e7c000 3f3e000 1f9f000 fcf800 7e7c00 3f3e00 1f9f00 fcf80 7e7c0 3f3e0
  //   1f9f0 fcf8 7e7c 3f3e 1f9f fcf 7e7 3f3 1f9 fc 7e 3f 1f f 7 3 1 0 0 0 0 0 0 0 0 0 0 0 0 0 0 0 0 0 0 0
  //   0 0 0 0 0 0  0 0 0 0 0 0 0 0 0 0 0 0 0 0 0 0 0 0 0 0 0 0 0 0 0 0 0 0 0 0 0 0 0 0 0 0 0 0 0 0
  //   47b10000 a3d88000 d1ec4000 68f62000 347b1000 9a3d8800 cd1ec400 668f6200 3347b100 99a3d880 ccd1ec40
  //   6668f620 b3347b10 599a3d88 2ccd1ec4 16668f62 8b3347b1 c599a3d9 e2ccd1ed f16668f7 f8b3347c fc599a3e
  //   fe2ccd1f ff166690 ff8b3348 ffc599a4 ffe2ccd2 fff16669 fff8b335 fffc599b fffe2cce ffff1667 7ffb0000
  //   3ffd8000 1ffec000 fff6000 7ffb000 3ffd800 1ffec00 fff600 7ffb00 3ffd80 1ffec0 fff60 7ffb0 3ffd8
  //   1ffec fff6 7ffb 3ffd 1ffe fff 7ff 3ff 1ff ff 7f 3f 1f f 7 3 1 0 fd400000 fea00000 7f500000 3fa80000
  //   1fd40000 8fea0000 47f50000 a3fa8000 d1fd4000 e8fea000 f47f5000 fa3fa800 fd1fd400 7e8fea00 bf47f500
  //   dfa3fa80 6fd1fd40 37e8fea0 1bf47f50 dfa3fa8 6fd1fd4 37e8fea 1bf47f5 dfa3fa 6fd1fd 37e8fe 1bf47f
  //   dfa3f 6fd1f 37e8f 1bf47 dfa3  0 0 0 0 0 0 0 0 0 0 0 0 0 0 0 0 0 0 0 0 0 0 0 0 0 0 0 0 0 0 0 0 0 0 0
  //   0 0 0 0 0 0 0 0 0 0 0 0 0 0 0 0 0 0 0 0 0 0 0 0 0 0 0 0 0 0 0 0 0 0 0 0 0 0 0 0 0 0 0 0 0 0 0 0 0 0
  //   0 0 0 0 0 0 0 0 0 0 0
  //   contents of rom_5 (hex, n*v repeats v):
  //   100000 80000 40000 20000 10000 8000 4000 2000 1000 800 400 200 100 80 40 20 10 8 4 2 1 0 0 0 0 0 0 0
  //   0 0 0 0 3ff80000 1ffc0000 ffe0000 7ff0000 3ff8000 1ffc000 ffe000 7ff000  3ff800 1ffc00 ffe00 7ff00
  //   3ff80 1ffc0 ffe0 7ff0 3ff8 1ffc ffe 7ff 3ff 1ff ff 7f 3f 1f f 7 3 1 0 0 10100000 8080000 4040000
  //   2020000 1010000 808000 404000 202000 101000 80800 40400 20200 10100 8080 4040 2020 1010 808 404 202
  //   101 80 40 20 10 8 4 2 1 0 0 0 54a40000 2a520000 15290000 a948000 54a4000 2a52000 1529000 a94800
  //   54a400 2a5200 152900 a9480 54a40 2a520 15290 a948 54a4 2a52 1529 a94 54a 2a5 152 a9 54 2a 15 a 5 2 1
  //   0 4a40000 2520000 1290000 948000 4a4000 252000 129000 94800 4a400 25200 12900 9480 4a40 2520 1290
  //   948 4a4 252 129 94 4a 25 12 9 4 2 1 0 0 0 0 0 1f100000 f880000 7c40000 3e20000 1f10000 f88000 7c4000
  //   3e2000  1f1000 f8800 7c400 3e200 1f100 f880 7c40 3e20 1f10 f88 7c4 3e2 1f1 f8 7c 3e 1f f 7 3 1 0 0 0
  //   11200000 8900000 4480000 2240000 1120000 890000 448000 224000 112000 89000 44800 22400 11200 8900
  //   4480 2240 1120 890 448 224 112 89 44 22 11 8 4 2 1 0 0 0 42840000 21420000 10a10000 8508000 4284000
  //   2142000 10a1000 850800 428400 214200 10a100 85080 42840 21420 10a10 8508 4284 2142 10a1 850 428 214
  //   10a 85 42 21 10 8 4 2 1 0 0 0 0 0 0 0 0 0 0 0 0 0 0 0 0 0 0 0 0 0 0 0 0 0 0 0 0 0 0 0 0 0 0 0 0 0 0
  //   0 0 0 0 0 0 0 0 0 0 0  0 0 0 0 0 0 0 0 0 0 0 0 0 0 0 0 47b10000 a3d88000 d1ec4000 68f62000 347b1000
  //   9a3d8800 cd1ec400 668f6200 3347b100 99a3d880 ccd1ec40 6668f620 b3347b10 599a3d88 2ccd1ec4 16668f62
  //   8b3347b1 c599a3d9 e2ccd1ed f16668f7 f8b3347c fc599a3e fe2ccd1f ff166690 ff8b3348 ffc599a4 ffe2ccd2
  //   fff16669 fff8b335 fffc599b fffe2cce ffff1667 7ffb0000 3ffd8000 1ffec000 fff6000 7ffb000 3ffd800
  //   1ffec00 fff600 7ffb00 3ffd80 1ffec0 fff60 7ffb0 3ffd8 1ffec fff6 7ffb 3ffd 1ffe fff 7ff 3ff 1ff ff
  //   7f 3f 1f f 7 3 1 0 fd400000 fea00000 7f500000 3fa80000 1fd40000 8fea0000 47f50000 a3fa8000 d1fd4000
  //   e8fea000 f47f5000 fa3fa800 fd1fd400 7e8fea00 bf47f500 dfa3fa80 6fd1fd40 37e8fea0 1bf47f50 dfa3fa8
  //   6fd1fd4 37e8fea 1bf47f5 dfa3fa 6fd1fd 37e8fe 1bf47f dfa3f 6fd1f 37e8f 1bf47 dfa3 0 0 0 0 0 0 0 0  0
  //   0 0 0 0 0 0 0 0 0 0 0 0 0 0 0 0 0 0 0 0 0 0 0 0 0 0 0 0 0 0 0 0 0 0 0 0 0 0 0 0 0 0 0 0 0 0 0 0 0 0
  //   0 0 0 0 0 0 0 0 0 0 0 0 0 0 0 0 0 0 0 0 0 0 0 0 0 0 0 0 0 0 0 0 0 0 0 0 0
  //   contents of rom_6 (hex, n*v repeats v):
  //   2100000 1080000 840000 420000 210000 108000 84000 42000 21000 10800 8400 4200 2100 1080 840 420 210
  //   108 84 42 21 10 8 4 2 1 0 0 0 0 0 0 21080000 10840000 8420000 4210000 2108000 1084000 842000 421000
  //   210800 108400 84200 42100 21080 10840 8420 4210 2108 1084 842 421 210 108 84 42  21 10 8 4 2 1 0 0
  //   10100000 8080000 4040000 2020000 1010000 808000 404000 202000 101000 80800 40400 20200 10100 8080
  //   4040 2020 1010 808 404 202 101 80 40 20 10 8 4 2 1 0 0 0 58a20000 2c510000 16288000 b144000 58a2000
  //   2c51000 1628800 b14400 58a200 2c5100 162880 b1440 58a20 2c510 16288 b144 58a2 2c51 1628 b14 58a 2c5
  //   162 b1 58 2c 16 b 5 2 1 0 4840000 2420000 1210000 908000 484000 242000 121000 90800 48400 24200
  //   12100 9080 4840 2420 1210 908 484 242 121 90 48 24 12 9 4 2 1 0 0 0 0 0 11100000 8880000 4440000
  //   2220000 1110000 888000 444000 222000 111000 88800 44400 22200 11100 8880 4440 2220  1110 888 444 222
  //   111 88 44 22 11 8 4 2 1 0 0 0 7ffe0000 3fff0000 1fff8000 fffc000 7ffe000 3fff000 1fff800 fffc00
  //   7ffe00 3fff00 1fff80 fffc0 7ffe0 3fff0 1fff8 fffc 7ffe 3fff 1fff fff 7ff 3ff 1ff ff 7f 3f 1f f 7 3 1
  //   0 42840000 21420000 10a10000 8508000 4284000 2142000 10a1000 850800 428400 214200 10a100 85080 42840
  //   21420 10a10 8508 4284 2142 10a1 850 428 214 10a 85 42 21 10 8 4 2 1 0 0 0 0 0 0 0 0 0 0 0 0 0 0 0 0
  //   0 0 0 0 0 0 0 0 0 0 0 0 0 0 0 0 0 0 0 0 0 0 0 0 0 0 0 0 0 0 0 0 0 0 0 0 0 0 0 0 0 0 0 0 0 0 0 0 0
  //   47b10000 a3d88000 d1ec4000 68f62000 347b1000 9a3d8800 cd1ec400 668f6200 3347b100 99a3d880 ccd1ec40
  //   6668f620 b3347b10 599a3d88 2ccd1ec4 16668f62 8b3347b1 c599a3d9 e2ccd1ed f16668f7 f8b3347c fc599a3e
  //   fe2ccd1f ff166690 ff8b3348 ffc599a4 ffe2ccd2 fff16669 fff8b335 fffc599b fffe2cce ffff1667 7ffb0000
  //   3ffd8000 1ffec000 fff6000 7ffb000 3ffd800 1ffec00 fff600 7ffb00 3ffd80 1ffec0 fff60 7ffb0 3ffd8
  //   1ffec fff6 7ffb 3ffd 1ffe fff 7ff 3ff 1ff ff 7f 3f 1f f 7 3 1 0 fd400000 fea00000 7f500000 3fa80000
  //   1fd40000 8fea0000 47f50000 a3fa8000 d1fd4000 e8fea000 f47f5000 fa3fa800 fd1fd400 7e8fea00 bf47f500
  //   dfa3fa80 6fd1fd40 37e8fea0 1bf47f50 dfa3fa8 6fd1fd4 37e8fea 1bf47f5 dfa3fa 6fd1fd 37e8fe 1bf47f
  //   dfa3f 6fd1f 37e8f 1bf47 dfa3 0 0 0 0 0 0 0 0 0 0 0 0 0 0 0 0 0 0 0 0 0 0 0 0 0 0 0 0 0 0 0 0 0 0 0 0
  //   0 0 0 0  0 0 0 0 0 0 0 0 0 0 0 0 0 0 0 0 0 0 0 0 0 0 0 0 0 0 0 0 0 0 0 0 0 0 0 0 0 0 0 0 0 0 0 0 0 0
  //   0 0 0 0 0 0 0 0 0 0
  //   contents of rom_7 (hex, n*v repeats v):
  //   f1200000 78900000 3c480000 1e240000 f120000 7890000 3c48000 1e24000 f12000 789000 3c4800 1e2400
  //   f1200 78900 3c480 1e240 f120 7890 3c48 1e24 f12 789 3c4 1e2 f1 78 3c 1e f 7 3 1 21080000 10840000
  //   8420000 4210000 2108000 1084000 842000 421000 210800 108400 84200 42100 21080 10840 8420 4210 2108
  //   1084 842 421 210 108 84 42 21 10 8 4 2 1 0 0 1ff00000 ff80000 7fc0000 3fe0000 1ff0000 ff8000 7fc000
  //   3fe000 1ff000 ff800 7fc00 3fe00 1ff00 ff80 7fc0 3fe0  1ff0 ff8 7fc 3fe 1ff ff 7f 3f 1f f 7 3 1 0 0 0
  //   51220000 28910000 14488000 a244000 5122000 2891000 1448800 a24400 512200 289100 144880 a2440 51220
  //   28910 14488 a244 5122 2891 1448 a24 512 289 144 a2 51 28 14 a 5 2 1 0 48940000 244a0000 12250000
  //   9128000 4894000 244a000 1225000 912800 489400 244a00 122500 91280 48940 244a0 12250 9128 4894 244a
  //   1225 912 489 244 122 91 48 24 12 9 4 2 1 0 11100000 8880000 4440000 2220000 1110000 888000 444000
  //   222000 111000 88800 44400 22200 11100 8880 4440 2220 1110 888 444 222 111 88 44 22 11 8 4 2 1 0 0 0
  //   42020000 21010000 10808000 8404000 4202000 2101000 1080800 840400 420200 210100 108080 84040 42020
  //   21010 10808 8404  4202 2101 1080 840 420 210 108 84 42 21 10 8 4 2 1 0 43040000 21820000 10c10000
  //   8608000 4304000 2182000 10c1000 860800 430400 218200 10c100 86080 43040 21820 10c10 8608 4304 2182
  //   10c1 860 430 218 10c 86 43 21 10 8 4 2 1 0 0 0 0 0 0 0 0 0 0 0 0 0 0 0 0 0 0 0 0 0 0 0 0 0 0 0 0 0 0
  //   0 0 0 0 0 0 0 0 0 0 0 0 0 0 0 0 0 0 0 0 0 0 0 0 0 0 0 0 0 0 0 0 0 0 0 47b10000 a3d88000 d1ec4000
  //   68f62000 347b1000 9a3d8800 cd1ec400 668f6200 3347b100 99a3d880 ccd1ec40 6668f620 b3347b10 599a3d88
  //   2ccd1ec4 16668f62 8b3347b1 c599a3d9 e2ccd1ed f16668f7 f8b3347c fc599a3e fe2ccd1f ff166690 ff8b3348
  //   ffc599a4 ffe2ccd2 fff16669 fff8b335 fffc599b fffe2cce ffff1667  7ffb0000 3ffd8000 1ffec000 fff6000
  //   7ffb000 3ffd800 1ffec00 fff600 7ffb00 3ffd80 1ffec0 fff60 7ffb0 3ffd8 1ffec fff6 7ffb 3ffd 1ffe fff
  //   7ff 3ff 1ff ff 7f 3f 1f f 7 3 1 0 fd400000 fea00000 7f500000 3fa80000 1fd40000 8fea0000 47f50000
  //   a3fa8000 d1fd4000 e8fea000 f47f5000 fa3fa800 fd1fd400 7e8fea00 bf47f500 dfa3fa80 6fd1fd40 37e8fea0
  //   1bf47f50 dfa3fa8 6fd1fd4 37e8fea 1bf47f5 dfa3fa 6fd1fd 37e8fe 1bf47f dfa3f 6fd1f 37e8f 1bf47 dfa3 0
  //   0 0 0 0 0 0 0 0 0 0 0 0 0 0 0 0 0 0 0 0 0 0 0 0 0 0 0 0 0 0 0 0 0 0 0 0 0 0 0 0 0 0 0 0 0 0 0 0 0 0
  //   0 0 0 0 0 0 0 0 0 0 0 0 0 0 0 0 0 0 0 0 0  0 0 0 0 0 0 0 0 0 0 0 0 0 0 0 0 0 0 0 0 0 0 0 0
  //   contents of rom_8 (hex, n*v repeats v):
  //   10a00000 8500000 4280000 2140000 10a0000 850000 428000 214000 10a000 85000 42800 21400 10a00 8500
  //   4280 2140 10a0 850 428 214 10a 85 42 21 10 8 4 2 1 0 0 0 3ff80000 1ffc0000 ffe0000 7ff0000 3ff8000
  //   1ffc000 ffe000 7ff000 3ff800 1ffc00 ffe00 7ff00 3ff80 1ffc0 ffe0 7ff0 3ff8 1ffc ffe 7ff 3ff 1ff ff
  //   7f 3f 1f f 7 3 1 0 0 0 0 0 0 0 0 0 0 0 0 0 0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
  //   contents of rom_9 (hex, n*v repeats v):
  //   10400000 8200000 4100000 2080000 1040000 820000 410000 208000 104000 82000 41000 20800 10400 8200
  //   4100 2080 1040 820 410 208 104 82 41 20 10 8 4 2 1 0 0 0 1000000 800000 400000 200000 100000 80000
  //   40000 20000 10000 8000 4000 2000 1000 800 400 200 100 80 40 20 10 8 4 2 1 0 0 0 0 0 0 0 fffe0000
  //   7fff00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
  //   contents of rom_10 (hex, n*v repeats v):
  //   10a00000 8500000 4280000 2140000 10a0000 850000 428000 214000 10a000 85000 42800 21400 10a00 8500
  //   4280 2140 10a0 850 428 214 10a 85 42 21 10 8 4 2 1 0 0 0 1000000 800000 400000 200000 100000 80000
  //   40000 20000 10000 8000 4000 2000 1000 800 400 200 100 80 40 20 10 8 4 2 1 0 0 0 0 0 0 0  1000000
  //   800000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
  //   contents of rom_11 (hex, n*v repeats v):
  //   11100000 8880000 4440000 2220000 1110000 888000 444000 222000 111000 88800 44400 22200 11100 8880
  //   4440 2220 1110 888 444 222 111 88 44 22 11 8 4 2 1 0 0 0 3ff80000 1ffc0000 ffe0000 7ff0000 3ff8000
  //   1ffc000 ffe000 7ff000 3ff800 1ffc00 ffe00 7ff00 3ff80 1ffc0 ffe0 7ff0 3ff8 1ffc ffe 7ff 3ff 1ff ff
  //   7f 3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
  //   contents of rom_12 (hex, n*v repeats v):
  //   12080000 9040000 4820000 2410000 1208000 904000 482000 241000 120800 90400 48200 24100 12080 9040
  //   4820 2410 1208 904 482 241 120 90 48 24 12 9 4 2 1 0 0 0 1000000 800000 400000 200000 100000 80000
  //   40000 20000 10000 8000 4000 2000 1000 800 400 200 100 80 40 20 10 8 4 2 1 0 0 0 0 0 0 0 11f80000
  //   8fc000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
  //   contents of rom_13 (hex, n*v repeats v):
  //   14080000 a040000 5020000 2810000 1408000 a04000 502000 281000 140800 a0400 50200 28100 14080 a040
  //   5020 2810 1408 a04 502 281 140 a0 50 28 14 a 5 2 1 0 0 0 1000000 800000 400000 200000 100000 80000
  //   40000 20000 10000 8000 4000 2000 1000 800 400 200 100 80 40 20 10 8 4 2 1 0 0 0 0 0 0 0 11000000
  //   880000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
  //   contents of rom_14 (hex, n*v repeats v):
  //   28000000 14000000 a000000 5000000 2800000 1400000 a00000 500000 280000 140000 a0000 50000 28000
  //   14000 a000 5000 2800 1400 a00 500 280 140 a0 50 28 14 a 5 2 1 0 0 1000000 800000 400000 200000
  //   100000 80000 40000 20000 10000 8000 4000 2000 1000 800 400 200 100 80 40 20 10 8 4 2 1 0 0 0 0 0 0 0
  //   29000000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
  //   contents of rom_15 (hex, n*v repeats v):
  //   47fe0000 23ff0000 11ff8000 8ffc000 47fe000 23ff000 11ff800 8ffc00 47fe00 23ff00 11ff80 8ffc0 47fe0
  //   23ff0 11ff8 8ffc 47fe 23ff 11ff 8ff 47f 23f 11f 8f 47 23 11 8 4 2 1 0 fffe0000 7fff0000 3fff8000
  //   1fffc000 fffe000 7fff000 3fff800 1fffc00 fffe00 7fff00 3fff80 1fffc0 fffe0 7fff0 3fff8 1fffc fffe
  //   7fff 3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
  //   contents of rom_16 (hex, n*v repeats v):
  //   0 0 0 0 0 0 0 0  0 0 0 0 0 0 0 0 0 0 0 0 0 0 0 0 0 0 0 0 0 0 0 0 0 0 0 0 0 0 0 0 0 0 0 0 0 0 0 0 0 0
  //   0 0 0 0 0 0 0 0 0 0 0 0 0 0 83fe0000 41ff0000 20ff8000 107fc000 83fe000 41ff000 20ff800 107fc00
  //   83fe00 41ff00 20ff80 107fc0 83fe0 41ff0 20ff8 107fc 83fe 41ff 20ff 107f 83f 41f 20f 107 83 41 20 10
  //   8 4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
endmodule

module \_0_f计数器  (
  output [8:0] out_1
);

  wire button_1_out, clock_1_out;
  wire [8:0] adder_1_out;

  Adder #(.width(9)) adder_1 (.a(out_1), .b({9{1'b0}}), .out(adder_1_out), .cin(1'b1));  // open: cout
  Register #(.width(9)) register_1 (.D(adder_1_out), .en(1'b1), .Q(out_1), .clk(clock_1_out), .clr(button_1_out));
  Clock clock_1 (.out(clock_1_out));
  Button button_1 (.out(button_1_out));
endmodule
