// Logisim project T3.circ as structural Verilog: 1 circuit, main circuit main
module main (
  input  in_1,
  input  in_2,
  input  in_3,
  input  in_4,
  input  in_5,
  output out_6,
  output out_7,
  output \非门 
);

  wire transistor_1_out, transistor_9_out;

  Transistor #(.\type ("n")) transistor_1 (.in(1'b1), .out(transistor_1_out), .gate(in_1));
  Transistor #(.\type ("n")) transistor_2 (.in(transistor_1_out), .out(out_7), .gate(in_4));
  Transistor transistor_3 (.in(1'b0), .out(out_7), .gate(in_4));
  Transistor transistor_4 (.in(1'b0), .out(out_7), .gate(in_1));
  Transistor transistor_5 (.in(1'b1), .out(\非门 ), .gate(in_5));
  Transistor #(.\type ("n")) transistor_6 (.in(1'b0), .out(\非门 ), .gate(in_5));
  Transistor #(.\type ("n")) transistor_7 (.in(1'b1), .out(out_6), .gate(in_2));
  Transistor transistor_8 (.in(transistor_9_out), .out(out_6), .gate(in_3));
  Transistor transistor_9 (.in(1'b0), .out(transistor_9_out), .gate(in_2));
  Transistor #(.\type ("n")) transistor_10 (.in(1'b1), .out(out_6), .gate(in_3));

  // Notes on the sheet:
  //   与门
  //   张芷苒_PB21081601
  //   或门
  //   张芷苒_PB21081601
  //   张芷苒_PB21081601
endmodule
